// Logisim project Guia_1201.circ as structural Verilog: 2 circuits, main circuit main
module main (
  input  ADDR,
  input  R_W,
  input  CLK,
  input  CLEAR,
  input  x1,
  input  x2,
  input  x3,
  input  x4,
  output x1_2,
  output x2_2,
  output x3_2,
  output x4_2
);

  MEMORY memory_1 (.ADDR(ADDR), .R_W(R_W), .CLK(CLK), .IN(x1), .CLEAR(CLEAR), .out_6(x1_2));
  MEMORY memory_2 (.ADDR(ADDR), .R_W(R_W), .CLK(CLK), .IN(x2), .CLEAR(CLEAR), .out_6(x2_2));
  MEMORY memory_3 (.ADDR(ADDR), .R_W(R_W), .CLK(CLK), .IN(x3), .CLEAR(CLEAR), .out_6(x3_2));
  MEMORY memory_4 (.ADDR(ADDR), .R_W(R_W), .CLK(CLK), .IN(x4), .CLEAR(CLEAR), .out_6(x4_2));

  // Notes on the sheet:
  //   806454 - Yago Almeida Melo
endmodule

module MEMORY (
  input  ADDR,
  input  R_W,
  input  CLK,
  input  CLEAR,
  input  IN,
  output out_6
);

  wire and_1_out, j_k_ff_1_q, not_1_out;

  and and_1 (and_1_out, ADDR, R_W, CLK);
  not not_1 (not_1_out, IN);
  J_K_Flip_Flop j_k_ff_1 (.J(IN), .clk(and_1_out), .K(not_1_out), .Q(j_k_ff_1_q), .reset(CLEAR));  // open: Qn, preset
  and and_2 (out_6, ADDR, j_k_ff_1_q);

  // Notes on the sheet:
  //   806454 - Yago Almeida Melo
endmodule
