// Logisim project Guia_1202.circ as structural Verilog: 3 circuits, main circuit main
module main (
  input  ADDR,
  input  R_W,
  input  CLK,
  input  CLEAR,
  input  x1,
  input  x2,
  input  x2_2,
  input  x2_3,
  input  x2_4,
  input  x2_5,
  input  x2_6,
  input  x2_7,
  output out_13,
  output out_14,
  output out_15,
  output out_16,
  output out_17,
  output out_18,
  output out_19,
  output out_20
);

  RAM_1x4 ram_1x4_1 (
    .ADDR(ADDR), .R_W(R_W), .CLK(CLK), .s1(out_13), .s2(R_W), .s3(out_15), .s4(out_16), .CLEAR(CLEAR),
    .x1(x1), .x2(x2), .x3(x2_2), .x4(x2_3));
  RAM_1x4 ram_1x4_2 (
    .ADDR(ADDR), .R_W(R_W), .CLK(CLK), .s1(out_17), .s2(out_18), .s3(out_19), .s4(out_20), .CLEAR(CLEAR),
    .x1(x2_4), .x2(x2_5), .x3(x2_6), .x4(x2_7));

  assign out_14 = R_W;

  // Notes on the sheet:
  //   806454 - Yago Almeida Melo
endmodule

module MEMORY (
  input  ADDR,
  input  R_W,
  input  CLK,
  input  CLEAR,
  input  IN,
  output out_6
);

  wire and_1_out, j_k_ff_1_q, not_1_out;

  and and_1 (and_1_out, ADDR, R_W, CLK);
  not not_1 (not_1_out, IN);
  J_K_Flip_Flop j_k_ff_1 (.J(IN), .clk(and_1_out), .K(not_1_out), .Q(j_k_ff_1_q), .reset(CLEAR));  // open: Qn, preset
  and and_2 (out_6, ADDR, j_k_ff_1_q);

  // Notes on the sheet:
  //   806454 - Yago Almeida Melo
endmodule

module RAM_1x4 (
  input  ADDR,
  input  R_W,
  input  CLK,
  input  CLEAR,
  input  x1,
  input  x2,
  input  x3,
  input  x4,
  output s1,
  output s2,
  output s3,
  output s4
);

  MEMORY memory_1 (.ADDR(ADDR), .R_W(R_W), .CLK(CLK), .IN(x1), .CLEAR(CLEAR), .out_6(s1));
  MEMORY memory_2 (.ADDR(ADDR), .R_W(R_W), .CLK(CLK), .IN(x2), .CLEAR(CLEAR), .out_6(s2));
  MEMORY memory_3 (.ADDR(ADDR), .R_W(R_W), .CLK(CLK), .IN(x3), .CLEAR(CLEAR), .out_6(s3));
  MEMORY memory_4 (.ADDR(ADDR), .R_W(R_W), .CLK(CLK), .IN(x4), .CLEAR(CLEAR), .out_6(s4));

  // Notes on the sheet:
  //   806454 - Yago Almeida Melo
endmodule
