// Logisim project Guia_1203.circ as structural Verilog: 4 circuits, main circuit main
module main (
  input  ADDR,
  input  R_W,
  input  CLK,
  input  CLEAR,
  input  in_5,
  input  in_6,
  input  in_7,
  input  in_8,
  input  in_9,
  input  in_10,
  input  in_11,
  input  in_12,
  output [7:0] out_13
);

  wire demultiplexer_1_out0, demultiplexer_1_out1;
  wire [7:0] ram_1x8_1_out_13, ram_1x8_2_out_13;

  Demultiplexer #(.enable("false")) demultiplexer_1 (
    .out0(demultiplexer_1_out0), .out1(demultiplexer_1_out1), .in(1'b1), .sel(ADDR));
  RAM_1x8 ram_1x8_1 (
    .ADDR(demultiplexer_1_out0), .R_W(R_W), .CLK(CLK), .CLEAR(CLEAR), .out_13(ram_1x8_1_out_13), .x1(in_5),
    .x2(in_6), .x2_2(in_7), .x2_3(in_7), .x2_4(in_9), .x2_5(in_10), .x2_6(in_11), .x2_7(in_12));
  RAM_1x8 ram_1x8_2 (
    .ADDR(demultiplexer_1_out1), .R_W(R_W), .CLK(CLK), .CLEAR(CLEAR), .out_13(ram_1x8_2_out_13), .x1(in_5),
    .x2(in_6), .x2_2(in_7), .x2_3(in_7), .x2_4(in_9), .x2_5(in_10), .x2_6(in_11), .x2_7(in_12));
  Multiplexer #(.width(8), .enable("false")) multiplexer_1 (
    .in0(ram_1x8_1_out_13), .in1(ram_1x8_2_out_13), .out(out_13), .sel(ADDR));

  assign in_8 = in_7;

  // Notes on the sheet:
  //   806454 - Yago Almeida Melo
endmodule

module MEMORY (
  input  ADDR,
  input  R_W,
  input  CLK,
  input  CLEAR,
  input  IN,
  output out_6
);

  wire and_1_out, j_k_ff_1_q, not_1_out;

  and and_1 (and_1_out, ADDR, R_W, CLK);
  not not_1 (not_1_out, IN);
  J_K_Flip_Flop j_k_ff_1 (.J(IN), .clk(and_1_out), .K(not_1_out), .Q(j_k_ff_1_q), .reset(CLEAR));  // open: Qn, preset
  and and_2 (out_6, ADDR, j_k_ff_1_q);

  // Notes on the sheet:
  //   806454 - Yago Almeida Melo
endmodule

module RAM_1x8 (
  input  ADDR,
  input  R_W,
  input  CLK,
  input  CLEAR,
  input  x1,
  input  x2,
  input  x2_2,
  input  x2_3,
  input  x2_4,
  input  x2_5,
  input  x2_6,
  input  x2_7,
  output [7:0] out_13
);

  RAM_1x4 ram_1x4_1 (
    .ADDR(ADDR), .R_W(R_W), .CLK(CLK), .s1(out_13[7]), .s2(R_W), .s3(out_13[5]), .s4(out_13[4]),
    .CLEAR(CLEAR), .x1(x1), .x2(x2), .x3(x2_2), .x4(x2_3));
  RAM_1x4 ram_1x4_2 (
    .ADDR(ADDR), .R_W(R_W), .CLK(CLK), .s1(out_13[3]), .s2(out_13[2]), .s3(out_13[1]), .s4(out_13[0]),
    .CLEAR(CLEAR), .x1(x2_4), .x2(x2_5), .x3(x2_6), .x4(x2_7));

  assign out_13[6] = R_W;

  // Notes on the sheet:
  //   806454 - Yago Almeida Melo
endmodule

module RAM_1x4 (
  input  ADDR,
  input  R_W,
  input  CLK,
  input  CLEAR,
  input  x1,
  input  x2,
  input  x3,
  input  x4,
  output s1,
  output s2,
  output s3,
  output s4
);

  MEMORY memory_1 (.ADDR(ADDR), .R_W(R_W), .CLK(CLK), .IN(x1), .CLEAR(CLEAR), .out_6(s1));
  MEMORY memory_2 (.ADDR(ADDR), .R_W(R_W), .CLK(CLK), .IN(x2), .CLEAR(CLEAR), .out_6(s2));
  MEMORY memory_3 (.ADDR(ADDR), .R_W(R_W), .CLK(CLK), .IN(x3), .CLEAR(CLEAR), .out_6(s3));
  MEMORY memory_4 (.ADDR(ADDR), .R_W(R_W), .CLK(CLK), .IN(x4), .CLEAR(CLEAR), .out_6(s4));

  // Notes on the sheet:
  //   806454 - Yago Almeida Melo
endmodule
