// Logisim project Guia_1205.circ as structural Verilog: 6 circuits, main circuit main
module main (
  input  ADDR1,
  input  ADDR2,
  input  ADDR3,
  input  R_W,
  input  CLK,
  input  CLEAR,
  input  [7:0] in_7,
  output [7:0] out_8
);

  RAM_4x8 ram_4x8_1 (.ADDR1(ADDR2), .ADDR2(ADDR3), .R_W(R_W), .CLK(CLK), .CLEAR(CLEAR), .in_6(in_7));  // open: out_7
  RAM_4x8 ram_4x8_2 (.ADDR1(ADDR2), .ADDR2(ADDR3), .R_W(R_W), .CLK(CLK), .CLEAR(CLEAR), .in_6(in_7));  // open: out_7
  Multiplexer #(.select(3), .width(8), .enable("false")) multiplexer_1 (
    .out(out_8), .sel({ADDR3, ADDR2, ADDR1}));  // open: in0, in1, in2, in3, in4, in5, in6, in7

  // Notes on the sheet:
  //   806454 - Yago Almeida Melo
endmodule

module RAM_1x4 (
  input  ADDR,
  input  R_W,
  input  CLK,
  input  CLEAR,
  input  [3:0] IN,
  output [3:0] out_6
);

  MEMORY memory_1 (.ADDR(ADDR), .R_W(R_W), .CLK(CLK), .IN(IN[3]), .CLEAR(CLEAR), .out_6(out_6[3]));
  MEMORY memory_2 (.ADDR(ADDR), .R_W(R_W), .CLK(CLK), .IN(IN[2]), .CLEAR(CLEAR), .out_6(out_6[2]));
  MEMORY memory_3 (.ADDR(ADDR), .R_W(R_W), .CLK(CLK), .IN(IN[1]), .CLEAR(CLEAR), .out_6(out_6[1]));
  MEMORY memory_4 (.ADDR(ADDR), .R_W(R_W), .CLK(CLK), .IN(IN[0]), .CLEAR(CLEAR), .out_6(out_6[0]));

  // Notes on the sheet:
  //   806454 - Yago Almeida Melo
endmodule

module RAM_1x8 (
  input  ADDR,
  input  R_W,
  input  CLK,
  input  [7:0] in_4,
  input  CLEAR,
  output [7:0] out_6
);

  RAM_1x4 ram_1x4_1 (.ADDR(ADDR), .R_W(R_W), .CLK(CLK), .IN(in_4[7:4]), .out_6(out_6[7:4]), .CLEAR(CLEAR));
  RAM_1x4 ram_1x4_2 (.ADDR(ADDR), .R_W(R_W), .CLK(CLK), .IN(in_4[3:0]), .out_6(out_6[3:0]), .CLEAR(CLEAR));

  // Notes on the sheet:
  //   806454 - Yago Almeida Melo
endmodule

module RAM_2x8 (
  input  ADDR,
  input  R_W,
  input  CLK,
  input  [7:0] in_4,
  input  CLEAR,
  output [7:0] out_6
);

  wire demultiplexer_1_out0, demultiplexer_1_out1;
  wire [7:0] ram_1x8_1_out_6, ram_1x8_2_out_6;

  Demultiplexer #(.enable("false")) demultiplexer_1 (
    .out0(demultiplexer_1_out0), .out1(demultiplexer_1_out1), .in(1'b1), .sel(ADDR));
  RAM_1x8 ram_1x8_1 (
    .ADDR(demultiplexer_1_out0), .R_W(R_W), .CLK(CLK), .in_4(in_4), .out_6(ram_1x8_1_out_6), .CLEAR(CLEAR));
  RAM_1x8 ram_1x8_2 (
    .ADDR(demultiplexer_1_out1), .R_W(R_W), .CLK(CLK), .in_4(in_4), .out_6(ram_1x8_2_out_6), .CLEAR(CLEAR));
  Multiplexer #(.width(8), .enable("false")) multiplexer_1 (
    .in1(ram_1x8_2_out_6), .out(out_6), .sel(ADDR));  // open: in0

  // Notes on the sheet:
  //   806454 - Yago Almeida Melo
endmodule

module RAM_4x8 (
  input  ADDR1,
  input  ADDR2,
  input  R_W,
  input  CLK,
  input  CLEAR,
  input  [7:0] in_6,
  output [7:0] out_7
);

  wire [7:0] ram_2x8_1_out_6, ram_2x8_2_out_6;

  RAM_2x8 ram_2x8_1 (.ADDR(ADDR1), .R_W(R_W), .CLK(CLK), .in_4(in_6), .CLEAR(CLEAR), .out_6(ram_2x8_1_out_6));
  RAM_2x8 ram_2x8_2 (.ADDR(ADDR1), .R_W(R_W), .CLK(CLK), .in_4(in_6), .CLEAR(CLEAR), .out_6(ram_2x8_2_out_6));
  Multiplexer #(.width(8), .enable("false")) multiplexer_1 (
    .in0(ram_2x8_1_out_6), .in1(ram_2x8_2_out_6), .out(out_7), .sel(ADDR2));

  // Notes on the sheet:
  //   806454 - Yago Almeida Melo
endmodule

module MEMORY (
  input  ADDR,
  input  R_W,
  input  CLK,
  input  CLEAR,
  input  IN,
  output out_6
);

  wire and_1_out, j_k_ff_1_q, not_1_out;

  and and_1 (and_1_out, ADDR, R_W, CLK);
  not not_1 (not_1_out, IN);
  J_K_Flip_Flop j_k_ff_1 (.J(IN), .clk(and_1_out), .K(not_1_out), .Q(j_k_ff_1_q), .reset(CLEAR));  // open: Qn, preset
  and and_2 (out_6, ADDR, j_k_ff_1_q);

  // Notes on the sheet:
  //   806454 - Yago Almeida Melo
endmodule
