// Logisim project Guia_1301.circ as structural Verilog: 1 circuit, main circuit main
module main (
  input  in,
  input  CLR,
  output out_3,
  output out_4,
  output out_5,
  output out_6,
  output out_7,
  output out_8
);

  wire CLK_p1;

  // ProgrammableGenerator CLK: pin names not known; wires that end beside it: CLK_p1
  J_K_Flip_Flop #(.Pre_Clr_Positions("LEGACY"), .NewFFLayout("false")) j_k_ff_1 (
    .J(in), .clk(out_4), .K(in), .Qn(out_3), .reset(CLR));  // open: Q, preset
  J_K_Flip_Flop #(.Pre_Clr_Positions("LEGACY"), .NewFFLayout("false")) j_k_ff_2 (
    .J(in), .clk(out_5), .K(in), .Qn(out_4), .reset(CLR));  // open: Q, preset
  J_K_Flip_Flop #(.Pre_Clr_Positions("LEGACY"), .NewFFLayout("false")) j_k_ff_3 (
    .J(in), .clk(out_6), .K(in), .Qn(out_5), .reset(CLR));  // open: Q, preset
  J_K_Flip_Flop #(.Pre_Clr_Positions("LEGACY"), .NewFFLayout("false")) j_k_ff_4 (
    .J(in), .clk(out_7), .K(in), .Qn(out_6), .reset(CLR));  // open: Q, preset
  J_K_Flip_Flop #(.Pre_Clr_Positions("LEGACY"), .NewFFLayout("false")) j_k_ff_5 (
    .J(in), .clk(out_8), .K(in), .Qn(out_7), .reset(CLR));  // open: Q, preset
  J_K_Flip_Flop #(.Pre_Clr_Positions("LEGACY"), .NewFFLayout("false")) j_k_ff_6 (
    .J(in), .clk(CLK_p1), .K(in), .Qn(out_8), .reset(CLR));  // open: Q, preset

  // Notes on the sheet:
  //   806454 - Yago Almeida Melo
endmodule
