// Logisim project Guia_1302.circ as structural Verilog: 1 circuit, main circuit main
module main (
  input  in,
  input  CLR,
  output out_3,
  output out_4,
  output out_5,
  output out_6,
  output out_7,
  output out_8
);

  wire CLK_p1, j_k_ff_2_q, j_k_ff_3_q, j_k_ff_4_q, j_k_ff_5_q, j_k_ff_6_q;

  // ProgrammableGenerator CLK: pin names not known; wires that end beside it: CLK_p1
  J_K_Flip_Flop #(.Pre_Clr_Positions("LEGACY"), .NewFFLayout("false")) j_k_ff_1 (
    .J(in), .clk(j_k_ff_2_q), .K(in), .Qn(out_3), .reset(CLR));  // open: Q, preset
  J_K_Flip_Flop #(.Pre_Clr_Positions("LEGACY"), .NewFFLayout("false")) j_k_ff_2 (
    .J(in), .clk(j_k_ff_3_q), .K(in), .Q(j_k_ff_2_q), .Qn(out_4), .reset(CLR));  // open: preset
  J_K_Flip_Flop #(.Pre_Clr_Positions("LEGACY"), .NewFFLayout("false")) j_k_ff_3 (
    .J(in), .clk(j_k_ff_4_q), .K(in), .Q(j_k_ff_3_q), .Qn(out_5), .reset(CLR));  // open: preset
  J_K_Flip_Flop #(.Pre_Clr_Positions("LEGACY"), .NewFFLayout("false")) j_k_ff_4 (
    .J(in), .clk(j_k_ff_5_q), .K(in), .Q(j_k_ff_4_q), .Qn(out_6), .reset(CLR));  // open: preset
  J_K_Flip_Flop #(.Pre_Clr_Positions("LEGACY"), .NewFFLayout("false")) j_k_ff_5 (
    .J(in), .clk(j_k_ff_6_q), .K(in), .Q(j_k_ff_5_q), .Qn(out_7), .reset(CLR));  // open: preset
  J_K_Flip_Flop #(.Pre_Clr_Positions("LEGACY"), .NewFFLayout("false")) j_k_ff_6 (
    .J(in), .clk(CLK_p1), .K(in), .Q(j_k_ff_6_q), .Qn(out_8), .reset(CLR));  // open: preset

  // Notes on the sheet:
  //   806454 - Yago Almeida Melo
endmodule
