// Logisim project Guia_1303.circ as structural Verilog: 1 circuit, main circuit main
module main (
  input  in_1,
  input  in_2,
  output out_3,
  output out_4,
  output out_5,
  output out_6
);

  wire j_k_ff_1_qn, j_k_ff_2_qn, j_k_ff_3_qn, nand_1_out, nand_2_out, not_1_out, not_2_out,
       programmablegenerator_1_p1;

  // ProgrammableGenerator programmablegenerator_1: pin names not known; wires that end beside it: programmablegenerator_1_p1
  nand nand_1 (nand_1_out, not_1_out, out_5, not_2_out, out_3);
  J_K_Flip_Flop #(.Pre_Clr_Positions("LEGACY"), .enable("true"), .NewFFLayout("false")) j_k_ff_1 (
    .J(in_1), .clk(programmablegenerator_1_p1), .K(in_1), .Q(out_6), .Qn(j_k_ff_1_qn), .reset(nand_2_out));  // open: preset, en
  nand nand_2 (nand_2_out, in_2, nand_1_out);
  not not_1 (not_1_out, out_6);
  not not_2 (not_2_out, out_4);
  J_K_Flip_Flop #(.Pre_Clr_Positions("LEGACY"), .enable("true"), .NewFFLayout("false")) j_k_ff_2 (
    .J(in_1), .clk(j_k_ff_1_qn), .K(in_1), .Q(out_5), .Qn(j_k_ff_2_qn), .reset(nand_2_out));  // open: preset, en
  J_K_Flip_Flop #(.Pre_Clr_Positions("LEGACY"), .enable("true"), .NewFFLayout("false")) j_k_ff_3 (
    .J(in_1), .clk(j_k_ff_2_qn), .K(in_1), .Q(out_4), .Qn(j_k_ff_3_qn), .reset(nand_2_out));  // open: preset, en
  J_K_Flip_Flop #(.Pre_Clr_Positions("LEGACY"), .enable("true"), .NewFFLayout("false")) j_k_ff_4 (
    .J(in_1), .clk(j_k_ff_3_qn), .K(in_1), .Q(out_3), .reset(nand_2_out));  // open: Qn, preset, en

  // Notes on the sheet:
  //   806454 - Yago Almeida Melo
endmodule
