// Logisim project Guia_1305.circ as structural Verilog: 1 circuit, main circuit main
module main (
  input  in_1,
  output out_2,
  output out_3,
  output out_4
);

  wire and_1_out, not_1_out, not_2_out, or_1_out, programmablegenerator_1_p1, t_ff_2_qn, t_ff_3_qn;

  // ProgrammableGenerator programmablegenerator_1: pin names not known; wires that end beside it: programmablegenerator_1_p1
  or or_1 (or_1_out, in_1, and_1_out);
  T_Flip_Flop #(.Pre_Clr_Positions("LEGACY"), .enable("true"), .NewFFLayout("false")) t_ff_1 (
    .clk(t_ff_2_qn), .T(t_ff_2_qn), .Q(out_2), .reset(or_1_out));  // open: Qn, preset, en
  not not_1 (not_1_out, out_2);
  and and_1 (and_1_out, not_1_out, out_3, not_2_out);
  not not_2 (not_2_out, out_4);
  T_Flip_Flop #(.Pre_Clr_Positions("LEGACY"), .enable("true"), .NewFFLayout("false")) t_ff_2 (
    .clk(t_ff_3_qn), .T(t_ff_3_qn), .Q(out_3), .Qn(t_ff_2_qn), .reset(or_1_out));  // open: preset, en
  T_Flip_Flop #(.Pre_Clr_Positions("LEGACY"), .enable("true"), .NewFFLayout("false")) t_ff_3 (
    .clk(programmablegenerator_1_p1), .T(programmablegenerator_1_p1), .Q(out_4), .Qn(t_ff_3_qn),
    .reset(or_1_out));  // open: preset, en

  // Notes on the sheet:
  //   806454 - Yago Almeida Melo
endmodule
