// Logisim project Guia_1401.circ as structural Verilog: 1 circuit, main circuit main
module main (
  input  in_1,
  input  in_2,
  input  in_3,
  output out_4,
  output out_5,
  output out_6,
  output out_7,
  output out_8
);

  D_Flip_Flop #(.Pre_Clr_Positions("LEGACY"), .enable("true"), .NewFFLayout("false")) d_ff_1 (
    .clk(in_1), .D(out_5), .Q(out_4), .reset(in_3));  // open: Qn, preset, en
  D_Flip_Flop #(.Pre_Clr_Positions("LEGACY"), .enable("true"), .NewFFLayout("false")) d_ff_2 (
    .clk(in_1), .D(out_6), .Q(out_5), .reset(in_3));  // open: Qn, preset, en
  D_Flip_Flop #(.Pre_Clr_Positions("LEGACY"), .enable("true"), .NewFFLayout("false")) d_ff_3 (
    .clk(in_1), .D(out_7), .Q(out_6), .reset(in_3));  // open: Qn, preset, en
  D_Flip_Flop #(.Pre_Clr_Positions("LEGACY"), .enable("true"), .NewFFLayout("false")) d_ff_4 (
    .clk(in_1), .D(out_8), .Q(out_7), .reset(in_3));  // open: Qn, preset, en
  D_Flip_Flop #(.Pre_Clr_Positions("LEGACY"), .enable("true"), .NewFFLayout("false")) d_ff_5 (
    .clk(in_1), .D(in_2), .Q(out_8), .reset(in_3));  // open: Qn, preset, en

  // Notes on the sheet:
  //   806454 - Yago Almeida Melo
endmodule
