// Logisim project (new)Guia_0402.circ as structural Verilog: 1 circuit, main circuit main
module main (
  input  x,
  input  y,
  output _2a,
  output _2b,
  output _2c,
  output _2d,
  output _2e
);

  wire and_1_out, and_2_out, and_3_out, not_1_out, not_2_out, not_3_out, not_4_out, not_5_out, not_6_out,
       not_7_out, not_8_out, not_9_out, not_10_out, not_11_out, not_12_out, not_13_out, not_14_out,
       not_15_out, or_1_out, or_2_out, or_3_out, or_4_out, or_5_out, or_6_out;

  not not_1 (not_1_out, x);
  not not_2 (not_2_out, y);
  not not_3 (not_3_out, x);
  not not_4 (not_4_out, x);
  not not_5 (not_5_out, y);
  not not_6 (not_6_out, x);
  not not_7 (not_7_out, y);
  not not_8 (not_8_out, x);
  not not_9 (not_9_out, y);
  not not_10 (not_10_out, x);
  not not_11 (not_11_out, y);
  or or_1 (or_1_out, not_1_out, not_2_out);
  or or_2 (or_2_out, not_3_out, y);
  and and_1 (and_1_out, x, y);
  and and_2 (and_2_out, not_4_out, y);
  or or_3 (or_3_out, x, not_5_out);
  and and_3 (and_3_out, not_6_out, not_7_out);
  or or_4 (or_4_out, not_8_out, not_9_out);
  or or_5 (or_5_out, not_10_out, y);
  or or_6 (or_6_out, x, not_11_out);
  not not_12 (not_12_out, or_1_out);
  or or_7 (_2b, or_2_out, and_1_out);
  not not_13 (not_13_out, and_2_out);
  not not_14 (not_14_out, and_3_out);
  not not_15 (not_15_out, or_4_out);
  and and_4 (_2a, not_12_out, x);
  and and_5 (_2c, not_13_out, or_3_out);
  or or_8 (_2d, not_14_out, not_15_out);
  and and_6 (_2e, or_5_out, or_6_out);

  // Notes on the sheet:
  //   806454 - Yago Almeida Melo
endmodule
