// Logisim project Guia_0401.circ as structural Verilog: 1 circuit, main circuit main
module main (
  input  x,
  input  y,
  input  z,
  input  x_2,
  input  y_2,
  input  z_2,
  input  x_3,
  input  y_3,
  input  z_3,
  input  x_4,
  input  y_4,
  input  z_4,
  input  x_5,
  input  y_5,
  input  z_5,
  output out_16,
  output out_17,
  output out_18,
  output out_19,
  output out_20
);

  wire nand_1_out, nand_2_out, nor_1_out, nor_2_out, not_1_out, not_2_out, not_3_out, not_4_out, not_5_out,
       not_6_out, not_7_out, not_8_out, not_9_out, not_10_out, or_1_out, or_2_out;

  not not_1 (not_1_out, y);
  not not_2 (not_2_out, z);
  not not_3 (not_3_out, x_2);
  not not_4 (not_4_out, x_3);
  not not_5 (not_5_out, y_3);
  not not_6 (not_6_out, z_3);
  not not_7 (not_7_out, y_4);
  not not_8 (not_8_out, x_5);
  not not_9 (not_9_out, y_5);
  not not_10 (not_10_out, z_5);
  nor nor_1 (nor_1_out, not_1_out, not_2_out);
  nor nor_2 (nor_2_out, not_3_out, y_2);
  nand nand_1 (nand_1_out, not_4_out, not_5_out);
  and and_1 (out_18, nand_1_out, not_6_out);
  nand nand_2 (nand_2_out, x_4, not_7_out);
  and and_2 (out_19, nand_2_out, z_4);
  or or_1 (or_1_out, not_8_out, y_5);
  or or_2 (or_2_out, not_9_out, not_10_out);
  and and_3 (out_16, x, nor_1_out);
  and and_4 (out_17, nor_2_out, z_2);
  and and_5 (out_20, or_1_out, or_2_out);

  // Notes on the sheet:
  //   1a)
  //   1b)
  //   1c)
  //   1d)
  //   1e)
  //   806454 - Yago Almeida Melo
endmodule
