// Logisim project Guia_0402.circ as structural Verilog: 1 circuit, main circuit main
module main (
  input  x,
  input  in_2,
  input  x_2,
  input  y,
  input  in_5,
  input  y_2,
  input  in_7,
  input  Simplificada,
  input  in_9,
  input  x_3,
  input  in_11,
  input  y_3,
  input  x_4,
  input  x_5,
  input  y_4,
  input  y_5,
  input  Simplificada_2,
  input  in_18,
  input  y_prime,
  output out_20,
  output out_21,
  output out_22,
  output out_23,
  output out_24,
  output out_25,
  output out_26,
  output out_27,
  output out_28,
  output out_29
);

  wire and_2_out, nand_1_out, nand_2_out, nor_1_out, nor_2_out, not_1_out, not_2_out, not_3_out, not_4_out,
       not_5_out, not_6_out, not_7_out, not_8_out, not_9_out, not_10_out, not_11_out, not_12_out, not_13_out,
       not_14_out, not_15_out, not_16_out, not_17_out, or_1_out, or_2_out, or_4_out, or_8_out;

  not not_1 (not_1_out, y_2);
  not not_2 (not_2_out, x_3);
  not not_3 (not_3_out, x_5);
  not not_4 (not_4_out, y_prime);
  not not_5 (not_5_out, x_2);
  or or_1 (or_1_out, x_2, not_1_out);
  not not_6 (not_6_out, or_1_out);
  and and_1 (out_25, not_2_out, y_3);
  or or_2 (or_2_out, not_3_out, not_7_out);
  not not_7 (not_7_out, y_5);
  and and_2 (and_2_out, not_7_out, x_5);
  and and_3 (out_29, 1'b1, not_4_out);
  and and_4 (out_20, not_5_out, not_6_out);
  or or_3 (out_27, or_2_out, and_2_out);
  nand nand_1 (nand_1_out, x, y);
  not not_8 (not_8_out, x);
  or or_4 (or_4_out, not_8_out, not_9_out);
  not not_9 (not_9_out, y);
  not not_10 (not_10_out, in_7);
  or or_5 (out_23, not_10_out, not_11_out);
  not not_11 (not_11_out, in_9);
  nand nand_2 (nand_2_out, x_4, y_4);
  nor nor_1 (nor_1_out, x_4, y_4);
  not not_12 (not_12_out, Simplificada_2);
  or or_6 (out_28, not_12_out, not_13_out);
  not not_13 (not_13_out, in_18);
  and and_5 (out_21, nand_1_out, or_4_out);
  or or_7 (out_26, nand_2_out, nor_1_out);
  not not_14 (not_14_out, Simplificada);
  not not_15 (not_15_out, in_11);
  nor nor_2 (nor_2_out, in_2, in_5);
  not not_16 (not_16_out, in_5);
  or or_8 (or_8_out, not_16_out, not_17_out);
  not not_17 (not_17_out, in_2);
  and and_6 (out_24, not_14_out, not_15_out);
  and and_7 (out_22, nor_2_out, or_8_out);

  // Notes on the sheet:
  //   2a)
  //   2b)
  //   Simplificada
  //   Simplificado
  //   Yago Almeida Melo - 806454
  //   $$
  //   2c)
  //   2d)
  //   Simplificada
  //   2e)
endmodule
