// Logisim project Guia_0405.circ as structural Verilog: 1 circuit, main circuit main
module main (
  input  x,
  input  y,
  input  x_2,
  input  x_3,
  input  y_2,
  input  y_3,
  input  x_4,
  input  y_4,
  input  z,
  input  x_5,
  input  y_5,
  input  z_2,
  output PoS,
  output out_14,
  output out_15,
  output out_16,
  output out_17
);

  wire not_1_out, not_2_out;

  or or_1 (PoS, x, y);
  and and_1 (out_14, x_2, y_2);
  not not_1 (not_1_out, z);
  and and_2 (out_16, x_4, y_4, not_1_out);
  and and_3 (out_17, x_5, y_5, z_2);
  not not_2 (not_2_out, y_3);
  or or_2 (out_15, x_3, not_2_out);

  // Notes on the sheet:
  //   5a)
  //   5b)
  //   5c)
  //   5d)
  //   806454 -Yago Almeida Melo
  //   SoP
  //   PoS
  //   PoS
  //   PoS
endmodule
