// Logisim project Guia_05.circ as structural Verilog: 1 circuit, main circuit main
module main (
  input  na,
  input  in_2,
  input  in_3,
  input  nb,
  input  a,
  input  in_6,
  input  in_7,
  input  nb_2,
  input  in_9,
  input  na_2,
  input  in_11,
  input  nb_3,
  input  in_13,
  input  na_3,
  input  in_15,
  input  b,
  input  in_17,
  input  in_18,
  input  in_19,
  input  _06,
  input  in_21,
  input  in_22,
  input  in_23,
  input  in_24,
  output out_25,
  output out_26,
  output out_27,
  output out_28,
  output out_29,
  output out_30,
  output out_31,
  output out_32,
  output out_33,
  output out_34,
  output out_35,
  output out_36
);

  wire and_2_out, not_1_out, not_2_out, not_3_out, not_4_out, not_5_out, not_6_out;

  not not_1 (not_1_out, na);
  and and_1 (out_25, not_1_out, not_2_out);
  not not_2 (not_2_out, nb);
  or or_1 (out_27, a, not_3_out);
  not not_3 (not_3_out, nb_2);
  not not_4 (not_4_out, na_2);
  or or_2 (out_30, not_4_out, not_5_out);
  not not_5 (not_5_out, nb_3);
  not not_6 (not_6_out, na_3);
  and and_2 (and_2_out, not_6_out, b);
  nor nor_1 (out_33, in_17, in_18);
  nand nand_1 (out_35, _06, in_22);
  nor nor_2 (out_36, in_23, in_24);
  not not_7 (out_32, and_2_out);
  nor nor_3 (out_26, in_2, in_3);
  nand nand_2 (out_28, in_6, in_7);
  nor nor_4 (out_29, in_9, in_11);
  nand nand_3 (out_31, in_13, in_15);
  nand nand_4 (out_34, in_19, in_21);

  // Notes on the sheet:
  //   01
  //   02
  //   03
  //   04
  //   05
  //   07
  //   08
endmodule
