// Logisim project Guia_0501.circ as structural Verilog: 3 circuits, main circuit main
module main (
  input  a,
  input  b,
  output out_3,
  output out_4
);

  a_b a_b_prime (.a(a), .b(b), .out_3(out_3));
  \nor  NOR (.a(a), .b(b), .out_3(out_4));

  // Notes on the sheet:
  //   806454 - Yago Almeida Melo
endmodule

module a_b (
  input  a,
  input  b,
  output out_3
);

  wire not_1_out;

  not not_1 (not_1_out, b);
  and and_1 (out_3, a, not_1_out);
endmodule

module \nor  (
  input  a,
  input  b,
  output out_3
);

  wire nor_1_out;

  nor nor_1 (nor_1_out, a, a);
  nor nor_2 (out_3, nor_1_out, b);
endmodule
