// Logisim project Guia_0502.circ as structural Verilog: 3 circuits, main circuit main
module main (
  input  a,
  input  b,
  output out_3,
  output out_4
);

  a__b a_prime_b (.a(a), .b(b), .out_3(out_3));
  NAND NAND (.a(a), .b(b), .out_3(out_4));

  // Notes on the sheet:
  //   806454 - Yago Almeida Melo
endmodule

module a__b (
  input  a,
  input  b,
  output out_3
);

  wire not_1_out;

  not not_1 (not_1_out, a);
  or or_1 (out_3, not_1_out, b);
endmodule

module NAND (
  input  a,
  input  b,
  output out_3
);

  wire nand_1_out;

  nand nand_1 (nand_1_out, b, b);
  nand nand_2 (out_3, a, nand_1_out);
endmodule
