// Logisim project Guia_0505.circ as structural Verilog: 3 circuits, main circuit main
module main (
  input  a,
  input  b,
  output out_3,
  output out_4
);

  a_b a_b_1 (.a(a), .b(b), .out_3(out_3));
  NOR nor_1 (.a(a), .b(b), .out_3(out_4));

  // Notes on the sheet:
  //   806454 - Yago Almeida Melo
endmodule

module a_b (
  input  a,
  input  b,
  output out_3
);

  xnor xnor_1 (out_3, a, b);
endmodule

module NOR (
  input  a,
  input  b,
  output out_3
);

  wire nor_1_out, nor_2_out, nor_3_out, nor_4_out;

  nor nor_1 (nor_1_out, a, a);
  nor nor_2 (nor_2_out, b, nor_1_out);
  nor nor_3 (nor_3_out, b, b);
  nor nor_4 (nor_4_out, a, nor_3_out);
  nor nor_5 (out_3, nor_2_out, nor_4_out);
endmodule
