// Logisim project Guia_0507.circ as structural Verilog: 3 circuits, main circuit main
module main (
  input  a,
  input  b,
  output out_3,
  output out_4
);

  a__b a_prime_b_prime__prime (.a(a), .b(b), .out_3(out_3));
  NOR NOR (.a(a), .b(b), .out_3(out_4));

  // Notes on the sheet:
  //   806454 - Yago Almeida Melo
endmodule

module NOR (
  input  a,
  input  b,
  output out_3
);

  wire nor_1_out, nor_2_out, nor_3_out, nor_5_out;

  nor nor_1 (nor_1_out, a, a);
  nor nor_2 (nor_2_out, b, b);
  nor nor_3 (nor_3_out, nor_1_out, b);
  nor nor_4 (out_3, nor_3_out, nor_5_out);
  nor nor_5 (nor_5_out, a, nor_2_out);
endmodule

module a__b (
  input  a,
  input  b,
  output out_3
);

  wire not_1_out, not_2_out;

  not not_1 (not_1_out, a);
  not not_2 (not_2_out, b);
  xnor xnor_1 (out_3, not_1_out, not_2_out);
endmodule
