// Logisim project Guia_0508.circ as structural Verilog: 3 circuits, main circuit main
module main (
  input  a,
  input  b,
  output out_3,
  output out_4
);

  a__b a_prime_b_prime__prime (.a(a), .b(b), .out_3(out_3));
  NAND NAND (.a(a), .b(b), .out_3(out_4));

  // Notes on the sheet:
  //   806454 - Yago Almeida Melo
endmodule

module a__b (
  input  a,
  input  b,
  output out_3
);

  wire and_1_out, not_1_out, not_2_out;

  not not_1 (not_1_out, a);
  not not_2 (not_2_out, b);
  not not_3 (out_3, and_1_out);
  and and_1 (and_1_out, not_1_out, not_2_out);
endmodule

module NAND (
  input  a,
  input  b,
  output out_3
);

  wire nand_1_out, nand_2_out;

  nand nand_1 (nand_1_out, a, a);
  nand nand_2 (nand_2_out, b, b);
  nand nand_3 (out_3, nand_1_out, nand_2_out);
endmodule
