// Logisim project Guia_0503.circ as structural Verilog: 3 circuits, main circuit main
module main (
  input  a,
  input  b,
  output out_3,
  output out_4
);

  a__b a_prime_b (.a(a), .b(b), .out_3(out_3));
  NOR NOR (.a(a), .b(b), .out_3(out_4));

  // Notes on the sheet:
  //   806454 - Yago Almeida Melo
endmodule

module a__b (
  input  a,
  input  b,
  output out_3
);

  wire not_1_out;

  not not_1 (not_1_out, a);
  or or_1 (out_3, not_1_out, b);
endmodule

module NOR (
  input  a,
  input  b,
  output out_3
);

  wire nor_1_out, nor_2_out;

  nor nor_1 (nor_1_out, a, a);
  nor nor_2 (nor_2_out, nor_1_out, b);
  nor nor_3 (out_3, nor_2_out, nor_2_out);
endmodule
