// Logisim project Guia_0504.circ as structural Verilog: 3 circuits, main circuit main
module main (
  input  a,
  input  b,
  output out_3,
  output out_4
);

  a_b a_b_1 (.a(a), .b(b), .out_3(out_3));
  NAND nand_1 (.a(a), .b(b), .out_3(out_4));

  // Notes on the sheet:
  //   806454 - Yago Almeida Melo
endmodule

module a_b (
  input  a,
  input  b,
  output out_3
);

  wire and_1_out, not_1_out;

  not not_1 (not_1_out, b);
  and and_1 (and_1_out, a, not_1_out);
  not not_2 (out_3, and_1_out);
endmodule

module NAND (
  input  a,
  input  b,
  output out_3
);

  wire nand_1_out;

  nand nand_1 (nand_1_out, b, b);
  nand nand_2 (out_3, a, nand_1_out);
endmodule
