// Logisim project Guia_0506.circ as structural Verilog: 3 circuits, main circuit main
module main (
  input  a,
  input  b,
  output out_3,
  output out_4
);

  a_b a_b_1 (.a(a), .b(b), .out_3(out_3));
  NAND nand_1 (.a(a), .b(b), .out_3(out_4));

  // Notes on the sheet:
  //   806454 - Yago Almeida Melo
endmodule

module NAND (
  input  a,
  input  b,
  output out_3
);

  wire nand_1_out, nand_2_out, nand_3_out, nand_4_out;

  nand nand_1 (nand_1_out, a, a);
  nand nand_2 (nand_2_out, b, b);
  nand nand_3 (nand_3_out, nand_1_out, b);
  nand nand_4 (nand_4_out, nand_2_out, a);
  nand nand_5 (out_3, nand_3_out, nand_4_out);
endmodule

module a_b (
  input  a,
  input  b,
  output out_3
);

  xor xor_1 (out_3, a, b);
endmodule
