// Logisim project Guia_0602.circ as structural Verilog: 1 circuit, main circuit main
module main (
  input  _2_a,
  input  y,
  input  in_3,
  input  x,
  input  y_2,
  input  z,
  input  c,
  input  y_3,
  input  z_2,
  input  x_2,
  input  y_4,
  input  z_3,
  input  x_3,
  input  y_5,
  input  z_4,
  output out_16,
  output out_17,
  output out_18,
  output out_19,
  output out_20,
  output out_21,
  output out_22,
  output out_23,
  output out_24,
  output out_25
);

  wire and_1_out, and_2_out, and_3_out, and_4_out, not_1_out, not_2_out, not_3_out, not_4_out, not_5_out,
       not_6_out, not_7_out, not_8_out, not_10_out, not_11_out, not_12_out, not_13_out, not_14_out,
       not_15_out, or_1_out, or_2_out, or_3_out, or_4_out, or_5_out, or_6_out, or_7_out, or_9_out, or_11_out,
       or_12_out, or_13_out, or_15_out, or_16_out, or_17_out, or_18_out, or_21_out, or_22_out, or_23_out,
       or_24_out;

  not not_1 (not_1_out, _2_a);
  not not_2 (not_2_out, x);
  not not_3 (not_3_out, c);
  not not_4 (not_4_out, x_2);
  not not_5 (not_5_out, in_3);
  not not_6 (not_6_out, y);
  not not_7 (not_7_out, y_2);
  not not_8 (not_8_out, y_3);
  not not_9 (out_23, y_4);
  not not_10 (not_10_out, y_5);
  not not_11 (not_11_out, x_3);
  or or_1 (or_1_out, _2_a, not_6_out, not_5_out);
  or or_2 (or_2_out, not_1_out, y, not_5_out);
  or or_3 (or_3_out, not_1_out, not_6_out, not_5_out);
  and and_1 (and_1_out, not_1_out, not_6_out);
  not not_12 (not_12_out, z);
  or or_4 (or_4_out, x, not_7_out, z);
  or or_5 (or_5_out, not_2_out, y_2, z);
  or or_6 (or_6_out, not_2_out, not_7_out, z);
  and and_2 (and_2_out, not_2_out, not_7_out);
  not not_13 (not_13_out, z_2);
  or or_7 (or_7_out, c, y_3, not_13_out);
  or or_8 (or_7_out, c, not_8_out, z_2);
  or or_9 (or_9_out, not_3_out, y_3, z_2);
  or or_10 (or_9_out, not_3_out, y_3, not_13_out);
  and and_3 (and_3_out, not_3_out, not_13_out);
  not not_14 (not_14_out, z_3);
  or or_11 (or_11_out, x_2, out_23, z_3);
  or or_12 (or_12_out, x_2, out_23, not_14_out);
  or or_13 (or_13_out, not_4_out, out_23, z_3);
  or or_14 (or_13_out, not_4_out, out_23, not_14_out);
  not not_15 (not_15_out, z_4);
  or or_15 (or_15_out, x_3, not_10_out, z_4);
  or or_16 (or_16_out, x_3, not_10_out, not_15_out);
  or or_17 (or_17_out, not_11_out, y_5, not_15_out);
  or or_18 (or_18_out, not_11_out, not_10_out, z_4);
  and and_4 (and_4_out, x_3, z_4);
  and and_5 (out_16, or_1_out, or_2_out, or_3_out);
  or or_19 (out_17, and_1_out, not_5_out);
  or or_20 (out_19, and_2_out, z);
  or or_21 (or_21_out, and_3_out, y_3);
  or or_22 (or_22_out, c, not_8_out, z_2);
  or or_23 (or_23_out, and_4_out, not_10_out);
  or or_24 (or_24_out, not_11_out, y_5, not_15_out);
  and and_6 (out_18, or_4_out, or_5_out, or_6_out);
  and and_7 (out_20, or_7_out, or_7_out, or_9_out, or_9_out);
  and and_8 (out_21, or_21_out, or_22_out);
  and and_9 (out_22, or_11_out, or_12_out, or_13_out, or_13_out);
  and and_10 (out_24, or_15_out, or_16_out, or_17_out, or_18_out);
  and and_11 (out_25, or_23_out, or_24_out);

  // Notes on the sheet:
  //   b)
  //   d)
  //   Guia 0602 
  //   806454 - Yago Ameida Melo
  //   x
  //   x
  //   e)
  //   z
endmodule
