// Logisim project Guia_0604.circ as structural Verilog: 1 circuit, main circuit main
module main (
  input  X,
  input  Y,
  input  W,
  input  Z,
  input  X_2,
  input  Y_2,
  input  W_2,
  input  Z_2,
  input  X_3,
  input  Y_3,
  input  W_3,
  input  Z_3,
  input  X_4,
  input  Y_4,
  input  W_4,
  input  Z_4,
  input  X_5,
  input  Y_5,
  input  W_5,
  input  Z_5,
  output out_21,
  output out_22,
  output out_23,
  output out_24,
  output out_25
);

  wire not_1_out, not_2_out, not_3_out, not_4_out, not_5_out, not_6_out, not_7_out, not_8_out, not_9_out,
       not_10_out, not_11_out, not_12_out, not_13_out, not_14_out, not_15_out, not_16_out, not_17_out,
       not_18_out, not_19_out, not_20_out, or_1_out, or_2_out, or_3_out, or_4_out, or_5_out, or_6_out,
       or_7_out, or_8_out, or_9_out, or_10_out, or_11_out, or_12_out, or_13_out, or_14_out, or_15_out,
       or_16_out, or_17_out, or_18_out, or_19_out, or_20_out;

  not not_1 (not_1_out, X);
  not not_2 (not_2_out, Y);
  not not_3 (not_3_out, Y_2);
  not not_4 (not_4_out, X_2);
  not not_5 (not_5_out, Y_3);
  not not_6 (not_6_out, X_3);
  not not_7 (not_7_out, Y_4);
  not not_8 (not_8_out, X_4);
  not not_9 (not_9_out, X_5);
  not not_10 (not_10_out, Y_5);
  not not_11 (not_11_out, W);
  not not_12 (not_12_out, W_2);
  not not_13 (not_13_out, W_3);
  not not_14 (not_14_out, W_4);
  not not_15 (not_15_out, W_5);
  not not_16 (not_16_out, Z);
  not not_17 (not_17_out, Z_2);
  not not_18 (not_18_out, Z_3);
  not not_19 (not_19_out, Z_4);
  not not_20 (not_20_out, Z_5);
  or or_1 (or_1_out, X, W);
  or or_2 (or_2_out, W, Z);
  or or_3 (or_3_out, Y, not_16_out);
  or or_4 (or_4_out, not_1_out, not_11_out);
  or or_5 (or_5_out, X_2, Y_2);
  or or_6 (or_6_out, not_12_out, Z_2);
  or or_7 (or_7_out, not_4_out, Z_2);
  or or_8 (or_8_out, not_3_out, W_2, not_17_out);
  or or_9 (or_9_out, X_3, Y_3);
  or or_10 (or_10_out, X_3, not_18_out);
  or or_11 (or_11_out, Y_3, not_18_out);
  or or_12 (or_12_out, not_13_out, Z_3);
  or or_13 (or_13_out, Y_4, Z_4);
  or or_14 (or_14_out, W_4, Z_4);
  or or_15 (or_15_out, not_8_out, Y_4);
  or or_16 (or_16_out, X_4, not_14_out, not_19_out);
  or or_17 (or_17_out, Y_5, W_5);
  or or_18 (or_18_out, Y_5, Z_5);
  or or_19 (or_19_out, W_5, Z_5);
  or or_20 (or_20_out, not_9_out, not_10_out, not_20_out);
  and and_1 (out_21, or_1_out, or_2_out, or_3_out, or_4_out);
  and and_2 (out_22, or_5_out, or_6_out, or_7_out, or_8_out);
  and and_3 (out_23, or_9_out, or_10_out, or_11_out, or_12_out);
  and and_4 (out_24, or_13_out, or_14_out, or_15_out, or_16_out);
  and and_5 (out_25, or_17_out, or_18_out, or_19_out, or_20_out);

  // Notes on the sheet:
  //   Guia_0604$806454 - Yago Almeida Melo
endmodule
