// Logisim project Guia_0605.circ as structural Verilog: 3 circuits, main circuit main
module main (
  input  in_1,
  input  in_2,
  input  in_3,
  output out_4,
  output out_5
);

  expression expression (.x(in_1), .y(in_2), .z(in_3), .out_4(out_4));
  Simplified Simplified (.x(in_1), .y(in_2), .z(in_3), .out_4(out_5));

  // Notes on the sheet:
  //   806454 - Yago Almeida Melo
endmodule

module expression (
  input  x,
  input  y,
  input  z,
  output out_4
);

  wire and_1_out, and_2_out, and_3_out, not_1_out, not_2_out, not_3_out, not_4_out, not_5_out, not_6_out,
       or_1_out, or_2_out;

  not not_1 (not_1_out, y);
  not not_2 (not_2_out, x);
  or or_1 (or_1_out, not_1_out, not_2_out);
  not not_3 (not_3_out, or_1_out);
  and and_1 (and_1_out, y, x);
  not not_4 (not_4_out, and_1_out);
  and and_2 (and_2_out, z, y);
  or or_2 (or_2_out, and_2_out, not_5_out);
  not not_5 (not_5_out, x);
  and and_3 (and_3_out, not_3_out, not_4_out);
  not not_6 (not_6_out, or_2_out);
  or or_3 (out_4, and_3_out, not_6_out);
endmodule

module Simplified (
  input  x,
  input  y,
  input  z,
  output out_4
);

  wire and_1_out, and_2_out, not_1_out, not_2_out;

  not not_1 (not_1_out, y);
  not not_2 (not_2_out, z);
  and and_1 (and_1_out, x, not_1_out);
  and and_2 (and_2_out, x, not_2_out);
  or or_1 (out_4, and_1_out, and_2_out);
endmodule
