// Logisim project Guia_0606.circ as structural Verilog: 3 circuits, main circuit main
module main (
  input  x,
  input  y,
  input  w,
  input  z,
  output out_5,
  output out_6
);

  expression expression (.x(x), .y(y), .w(w), .z(z), .out_5(out_5));
  simplified simplified (.x(x), .y(y), .w(w), .z(z), .out_5(out_6));

  // Notes on the sheet:
  //   806454 -  Yago Almeida Melo
endmodule

module expression (
  input  x,
  input  y,
  input  w,
  input  z,
  output out_5
);

  wire and_1_out, and_2_out, and_3_out, not_1_out, not_2_out, not_3_out, not_4_out, not_5_out, not_6_out,
       not_7_out, or_1_out, or_2_out;

  not not_1 (not_1_out, y);
  not not_2 (not_2_out, x);
  not not_3 (not_3_out, w);
  not not_4 (not_4_out, or_1_out);
  or or_1 (or_1_out, not_1_out, w, not_2_out);
  and and_1 (and_1_out, y, not_3_out, x);
  not not_5 (not_5_out, and_1_out);
  and and_2 (and_2_out, z, w, y);
  not not_6 (not_6_out, x);
  and and_3 (and_3_out, not_4_out, not_5_out);
  not not_7 (not_7_out, or_2_out);
  or or_2 (or_2_out, and_2_out, not_6_out);
  or or_3 (out_5, and_3_out, not_7_out);
endmodule

module simplified (
  input  x,
  input  y,
  input  w,
  input  z,
  output out_5
);

  wire not_1_out, not_2_out, not_3_out, not_4_out, or_1_out, or_2_out, or_3_out;

  or or_1 (or_1_out, x, y);
  or or_2 (or_2_out, x, not_1_out);
  not not_1 (not_1_out, y);
  not not_2 (not_2_out, y);
  or or_3 (or_3_out, not_2_out, not_3_out, not_4_out);
  not not_3 (not_3_out, w);
  not not_4 (not_4_out, z);
  and and_1 (out_5, or_1_out, or_2_out, or_3_out);
endmodule
