// Logisim project Guia_0607.circ as structural Verilog: 3 circuits, main circuit main
module main (
  input  x,
  input  y,
  input  z,
  output out_4,
  output out_5
);

  expression expression (.x(x), .y(y), .z(z), .out_4(out_4));
  simplified simplified (.x(x), .y(y), .z(z), .out_4(out_5));

  // Notes on the sheet:
  //   806454 - Yago Almeida Melo
endmodule

module simplified (
  input  x,
  input  y,
  input  z,
  output out_4
);

  wire not_1_out, not_2_out, or_1_out, or_2_out;

  not not_1 (not_1_out, y);
  not not_2 (not_2_out, x);
  or or_1 (or_1_out, x, not_1_out);
  or or_2 (or_2_out, not_2_out, y, z);
  and and_1 (out_4, or_1_out, or_2_out);
endmodule

module expression (
  input  x,
  input  y,
  input  z,
  output out_4
);

  wire not_1_out, not_2_out, not_3_out, not_4_out, or_1_out, or_2_out, or_3_out;

  or or_1 (or_1_out, x, not_1_out, not_2_out);
  not not_1 (not_1_out, y);
  not not_2 (not_2_out, z);
  not not_3 (not_3_out, x);
  or or_2 (or_2_out, not_3_out, y, z);
  not not_4 (not_4_out, y);
  or or_3 (or_3_out, x, not_4_out, z);
  and and_1 (out_4, or_1_out, or_2_out, or_3_out);
endmodule
