// Logisim project Guia_0608.circ as structural Verilog: 3 circuits, main circuit main
module main (
  input  w,
  input  x,
  input  y,
  input  z,
  output out_5,
  output out_6
);

  expression expression (.w(w), .x(x), .y(y), .z(z), .out_5(out_5));
  simplified simplified (.w(w), .x(x), .y(y), .z(z), .out_5(out_6));

  // Notes on the sheet:
  //   806454 - Yago Almeida Melo
endmodule

module expression (
  input  w,
  input  x,
  input  y,
  input  z,
  output out_5
);

  wire and_1_out, and_2_out, and_3_out, and_4_out, not_1_out, not_2_out, not_3_out, not_4_out, not_5_out,
       not_6_out, not_7_out;

  and and_1 (and_1_out, w, x, y, z);
  and and_2 (and_2_out, w, x, not_1_out, not_2_out);
  not not_1 (not_1_out, y);
  not not_2 (not_2_out, z);
  not not_3 (not_3_out, x);
  and and_3 (and_3_out, w, not_3_out, not_4_out, z);
  not not_4 (not_4_out, y);
  not not_5 (not_5_out, w);
  not not_6 (not_6_out, x);
  and and_4 (and_4_out, not_5_out, not_6_out, y, not_7_out);
  not not_7 (not_7_out, z);
  or or_1 (out_5, and_1_out, and_2_out, and_3_out, and_4_out);
endmodule

module simplified (
  input  w,
  input  x,
  input  y,
  input  z,
  output out_5
);

  wire and_1_out, and_2_out, and_3_out, not_1_out, not_2_out, not_3_out, not_4_out, not_5_out;

  and and_1 (and_1_out, w, x);
  not not_1 (not_1_out, x);
  and and_2 (and_2_out, w, not_1_out, not_2_out, z);
  not not_2 (not_2_out, y);
  not not_3 (not_3_out, w);
  not not_4 (not_4_out, x);
  and and_3 (and_3_out, not_3_out, not_4_out, y, not_5_out);
  not not_5 (not_5_out, z);
  or or_1 (out_5, and_1_out, and_2_out, and_3_out);
endmodule
