// Logisim project Guia_0701.circ as structural Verilog: 2 circuits, main circuit main
module main (
  input  a,
  input  b,
  input  select,
  output out_4
);

  LU lu_1 (.a(a), .b(b), .select(select), .out_4(out_4));

  // Notes on the sheet:
  //   806454 - Yago Almeida Melo
  //   0 = AND(a,b) / 1 = NAND(a,b)
endmodule

module LU (
  input  a,
  input  b,
  input  select,
  output out_4
);

  wire and_1_out, and_2_out, and_3_out, nand_1_out, not_1_out;

  and and_1 (and_1_out, a, b);
  nand nand_1 (nand_1_out, a, b);
  and and_2 (and_2_out, and_1_out, not_1_out);
  not not_1 (not_1_out, select);
  and and_3 (and_3_out, nand_1_out, select);
  or or_1 (out_4, and_2_out, and_3_out);
endmodule
