// Logisim project Guia_0702.circ as structural Verilog: 2 circuits, main circuit main
module main (
  input  a,
  input  b,
  input  select,
  output out_4
);

  LU lu_1 (.a(a), .b(b), .select(select), .out_4(out_4));

  // Notes on the sheet:
  //   806454 - Yago Almeida Melo
  //   0 = OR(a,b) / 1 = NOR(a,b)
endmodule

module LU (
  input  a,
  input  b,
  input  select,
  output out_4
);

  wire and_1_out, and_2_out, nor_1_out, not_1_out, or_1_out;

  or or_1 (or_1_out, a, b);
  nor nor_1 (nor_1_out, a, b);
  and and_1 (and_1_out, or_1_out, not_1_out);
  not not_1 (not_1_out, select);
  and and_2 (and_2_out, nor_1_out, select);
  or or_2 (out_4, and_1_out, and_2_out);
endmodule
