// Logisim project Guia_0704.circ as structural Verilog: 2 circuits, main circuit main
module main (
  input  a,
  input  b,
  input  chave1,
  input  chave2,
  output out_5
);

  LU lu_1 (.a(a), .b(b), .chave1(chave1), .chave2(chave2), .out_5(out_5));

  // Notes on the sheet:
  //   806454 - Yago Almeida Melo
endmodule

module LU (
  input  a,
  input  b,
  input  chave1,
  input  chave2,
  output out_5
);

  wire and_1_out, and_2_out, and_3_out, and_4_out, nor_1_out, not_1_out, not_2_out, not_3_out, not_4_out,
       or_1_out, xnor_1_out, xor_1_out;

  or or_1 (or_1_out, a, b);
  nor nor_1 (nor_1_out, a, b);
  xor xor_1 (xor_1_out, a, b);
  xnor xnor_1 (xnor_1_out, a, b);
  and and_1 (and_1_out, or_1_out, not_1_out, not_2_out);
  not not_1 (not_1_out, chave1);
  not not_2 (not_2_out, chave2);
  not not_3 (not_3_out, chave1);
  and and_2 (and_2_out, nor_1_out, not_3_out, chave2);
  and and_3 (and_3_out, xor_1_out, chave1, not_4_out);
  not not_4 (not_4_out, chave2);
  and and_4 (and_4_out, xnor_1_out, chave1, chave2);
  or or_2 (out_5, and_1_out, and_2_out, and_3_out, and_4_out);
endmodule
