// Logisim project Guia_0705.circ as structural Verilog: 2 circuits, main circuit main
module main (
  input  a,
  input  b,
  input  chave1,
  input  chave2,
  input  chave3,
  output out_6
);

  LU lu_1 (.a(a), .b(b), .chave1(chave1), .chave2(chave2), .chave3(chave3), .out_6(out_6));

  // Notes on the sheet:
  //   806454 - Yago Almeida Melo
endmodule

module LU (
  input  a,
  input  b,
  input  chave1,
  input  chave2,
  input  chave3,
  output out_6
);

  wire and_1_out, and_2_out, and_3_out, and_4_out, and_5_out, and_6_out, and_7_out, and_8_out, nand_1_out,
       nor_1_out, not_1_out, not_2_out, not_3_out, not_4_out, not_5_out, not_6_out, not_7_out, not_8_out,
       not_9_out, not_10_out, not_11_out, not_12_out, not_13_out, or_1_out, xnor_1_out, xor_1_out;

  not not_1 (not_1_out, b);
  and and_1 (and_1_out, a, b);
  nand nand_1 (nand_1_out, a, b);
  or or_1 (or_1_out, a, b);
  nor nor_1 (nor_1_out, a, b);
  xor xor_1 (xor_1_out, a, b);
  xnor xnor_1 (xnor_1_out, a, b);
  not not_2 (not_2_out, chave1);
  and and_2 (and_2_out, not_1_out, not_2_out, not_3_out, not_4_out);
  not not_3 (not_3_out, chave2);
  not not_4 (not_4_out, chave3);
  not not_5 (not_5_out, chave1);
  and and_3 (and_3_out, and_1_out, not_5_out, not_6_out, chave3);
  not not_6 (not_6_out, chave2);
  not not_7 (not_7_out, chave1);
  and and_4 (and_4_out, nand_1_out, not_7_out, chave2, not_8_out);
  not not_8 (not_8_out, chave3);
  not not_9 (not_9_out, chave1);
  and and_5 (and_5_out, or_1_out, not_9_out, chave2, chave3);
  and and_6 (and_6_out, nor_1_out, chave1, not_10_out, not_11_out);
  not not_10 (not_10_out, chave2);
  not not_11 (not_11_out, chave3);
  and and_7 (and_7_out, xor_1_out, chave1, not_12_out, chave3);
  not not_12 (not_12_out, chave2);
  and and_8 (and_8_out, xnor_1_out, chave1, chave2, not_13_out);
  not not_13 (not_13_out, chave3);
  or or_2 (out_6, and_2_out, and_3_out, and_4_out, and_5_out, and_6_out, and_7_out, and_8_out);
endmodule
