// Logisim project Guia_0801.circ as structural Verilog: 2 circuits, main circuit main
module main (
  input  A,
  input  B,
  input  VEM,
  output \Saída ,
  output Vai
);

  wire and_1_out, and_2_out, and_3_out, and_4_out, and_5_out, and_6_out, and_7_out, and_8_out, not_1_out,
       not_2_out, not_3_out, or_1_out, or_2_out, or_3_out, or_4_out;

  not not_1 (not_1_out, B);
  not not_2 (not_2_out, A);
  not not_3 (not_3_out, VEM);
  and and_1 (and_1_out, not_2_out, not_1_out, VEM);
  or or_1 (or_1_out, and_1_out, and_2_out);
  and and_2 (and_2_out, not_2_out, B, not_3_out);
  and and_3 (and_3_out, A, not_1_out, not_3_out);
  or or_2 (or_2_out, and_3_out, and_4_out);
  and and_4 (and_4_out, A, B, VEM);
  and and_5 (and_5_out, not_2_out, B, VEM);
  or or_3 (or_3_out, and_5_out, and_6_out);
  and and_6 (and_6_out, A, not_1_out, VEM);
  and and_7 (and_7_out, A, B, not_3_out);
  or or_4 (or_4_out, and_7_out, and_8_out);
  and and_8 (and_8_out, A, B, B);
  or or_5 (\Saída , or_1_out, or_2_out);
  or or_6 (Vai, or_3_out, or_4_out);

  // Notes on the sheet:
  //   Guia_0801
  //   806454 - Yago Almeida Melo
endmodule

module Soma (
  input  in_1,
  input  in_2,
  input  in_3,
  input  in_4,
  input  in_5,
  input  in_6,
  input  in_7,
  input  in_8,
  input  in_9,
  input  in_10,
  input  in_11,
  input  in_12,
  output out_13,
  output out_14,
  output out_15,
  output out_16,
  output out_17,
  output out_18
);

  wire main_2_vai, main_3_vai, main_4_vai, main_5_vai, main_6_vai;

  main main_1 (.\Saída (out_13), .A(in_1), .B(in_7), .VEM(main_2_vai));  // open: Vai
  main main_2 (.\Saída (out_14), .Vai(main_2_vai), .A(in_2), .B(in_8), .VEM(main_3_vai));
  main main_3 (.\Saída (out_15), .Vai(main_3_vai), .A(in_3), .B(in_9), .VEM(main_4_vai));
  main main_4 (.\Saída (out_16), .Vai(main_4_vai), .A(in_4), .B(in_10), .VEM(main_5_vai));
  main main_5 (.\Saída (out_17), .Vai(main_5_vai), .A(in_5), .B(in_11), .VEM(main_6_vai));
  main main_6 (.\Saída (out_18), .Vai(main_6_vai), .A(in_6), .B(in_12), .VEM(1'b0));

  // Notes on the sheet:
  //   A
  //   B
endmodule
