// Logisim project Guia_0803.circ as structural Verilog: 2 circuits, main circuit main
module main (
  input  in_1,
  input  in_2,
  input  A,
  input  in_4,
  input  in_5,
  input  in_6,
  input  in_7,
  input  in_8,
  input  in_9,
  input  in_10,
  input  in_11,
  input  in_12,
  output out_13
);

  wire comparator_1_igual, comparator_2_igual, comparator_3_igual, comparator_4_igual, comparator_5_igual,
       comparator_6_igual;

  comparator comparator_1 (.a(in_1), .b(in_7), .Igual(comparator_1_igual));  // open: a_b, a_b_2
  comparator comparator_2 (.a(in_2), .b(in_8), .Igual(comparator_2_igual));  // open: a_b, a_b_2
  comparator comparator_3 (.a(A), .b(in_9), .Igual(comparator_3_igual));  // open: a_b, a_b_2
  and and_1 (out_13, comparator_1_igual, comparator_2_igual, comparator_3_igual, comparator_4_igual, comparator_5_igual, comparator_6_igual);
  comparator comparator_4 (.a(in_4), .b(in_10), .Igual(comparator_4_igual));  // open: a_b, a_b_2
  comparator comparator_5 (.a(in_5), .b(in_11), .Igual(comparator_5_igual));  // open: a_b, a_b_2
  comparator comparator_6 (.a(in_6), .b(in_12), .Igual(comparator_6_igual));  // open: a_b, a_b_2

  // Notes on the sheet:
  //   806454 - Yago Almeida Melo
  //   B
endmodule

module comparator (
  input  a,
  input  b,
  output a_b,
  output Igual,
  output a_b_2
);

  wire not_1_out, not_2_out;

  not not_1 (not_1_out, a);
  not not_2 (not_2_out, b);
  and and_1 (a_b, not_1_out, b);
  xnor xnor_1 (Igual, a, b);
  and and_2 (a_b_2, not_2_out, a);
endmodule
