// Logisim project Guia_0804.circ as structural Verilog: 2 circuits, main circuit main
module main (
  input  in_1,
  input  in_2,
  input  A,
  input  in_4,
  input  in_5,
  input  in_6,
  input  in_7,
  input  in_8,
  input  in_9,
  input  in_10,
  input  in_11,
  input  in_12,
  output out_13
);

  wire desigualdade_1_diferente, desigualdade_2_diferente, desigualdade_3_diferente,
       desigualdade_4_diferente, desigualdade_5_diferente, desigualdade_6_diferente;

  Desigualdade desigualdade_1 (.a(in_1), .b(in_7), .Diferente(desigualdade_1_diferente));  // open: a_b, a_b_2
  Desigualdade desigualdade_2 (.a(in_2), .b(in_8), .Diferente(desigualdade_2_diferente));  // open: a_b, a_b_2
  Desigualdade desigualdade_3 (.a(A), .b(in_9), .Diferente(desigualdade_3_diferente));  // open: a_b, a_b_2
  or or_1 (out_13, desigualdade_1_diferente, desigualdade_2_diferente, desigualdade_3_diferente, desigualdade_4_diferente, desigualdade_5_diferente, desigualdade_6_diferente);
  Desigualdade desigualdade_4 (.a(in_4), .b(in_10), .Diferente(desigualdade_4_diferente));  // open: a_b, a_b_2
  Desigualdade desigualdade_5 (.a(in_5), .b(in_11), .Diferente(desigualdade_5_diferente));  // open: a_b, a_b_2
  Desigualdade desigualdade_6 (.a(in_6), .b(in_12), .Diferente(desigualdade_6_diferente));  // open: a_b, a_b_2

  // Notes on the sheet:
  //   806454 - Yago Almeida Melo
  //   B
endmodule

module Desigualdade (
  input  a,
  input  b,
  output a_b,
  output Diferente,
  output a_b_2
);

  wire not_1_out, not_2_out;

  not not_1 (not_1_out, a);
  not not_2 (not_2_out, b);
  and and_1 (a_b, not_1_out, b);
  xor xor_1 (Diferente, a, b);
  and and_2 (a_b_2, not_2_out, a);
endmodule
