// Logisim project Guia_0806.circ as structural Verilog
module main (
  input  in_1,
  input  in_2,
  input  in_3,
  input  in_4,
  input  in_5,
  input  in_6,
  input  in_7,
  input  in_8,
  input  in_9,
  input  in_10
);

  Soma soma_1 (
    .in_1(in_1), .in_2(in_2), .in_3(in_3), .in_4(in_4), .in_5(in_5), .in_6(in_6), .in_7(in_7), .in_8(in_8),
    .in_9(in_9), .in_10(in_10));  // open: out_11, out_12, out_13, out_14, out_15
endmodule

module halfAdder (
  input  x,
  input  y,
  input  vai_um,
  output s,
  output vem_um
);

  wire and_1_out, and_2_out, xor_1_out;

  xor xor_1 (xor_1_out, x, y);
  and and_1 (and_1_out, x, y);
  xor xor_2 (s, vai_um, xor_1_out);
  and and_2 (and_2_out, xor_1_out, vai_um);
  or or_1 (vem_um, and_2_out, and_1_out);
endmodule

module Soma (
  input  in_1,
  input  in_2,
  input  in_3,
  input  in_4,
  input  in_5,
  input  in_6,
  input  in_7,
  input  in_8,
  input  in_9,
  input  in_10,
  output out_11,
  output out_12,
  output out_13,
  output out_14,
  output out_15
);

  wire halfadder_2_vem_um, halfadder_3_vem_um, halfadder_4_vem_um, halfadder_5_vem_um;

  halfAdder halfadder_1 (.x(in_1), .y(in_6), .vai_um(halfadder_2_vem_um), .s(out_11));  // open: vem_um
  halfAdder halfadder_2 (.x(in_2), .y(in_7), .vai_um(halfadder_3_vem_um), .s(out_12), .vem_um(halfadder_2_vem_um));
  halfAdder halfadder_3 (.x(in_3), .y(in_8), .vai_um(halfadder_4_vem_um), .s(out_13), .vem_um(halfadder_3_vem_um));
  halfAdder halfadder_4 (.x(in_4), .y(in_9), .vai_um(halfadder_5_vem_um), .s(out_14), .vem_um(halfadder_4_vem_um));
  halfAdder halfadder_5 (.x(in_5), .y(in_10), .vai_um(1'b0), .s(out_15), .vem_um(halfadder_5_vem_um));

  // Notes on the sheet:
  //   806454 - Yago Almeida Melo
endmodule
