// Logisim project R01_01a.circ as structural Verilog: 1 circuit, main circuit main
module main (
  input  a,
  input  b,
  input  c,
  input  d,
  output out_5
);

  wire and_1_out, and_2_out, and_3_out, and_4_out, and_5_out, and_6_out, and_7_out, not_1_out, not_2_out,
       not_3_out, not_4_out;

  not not_1 (not_1_out, b);
  not not_2 (not_2_out, a);
  not not_3 (not_3_out, d);
  not not_4 (not_4_out, c);
  and and_1 (and_1_out, not_2_out, not_1_out, not_4_out, not_3_out);
  and and_2 (and_2_out, not_2_out, not_1_out, not_4_out, d);
  and and_3 (and_3_out, not_2_out, not_1_out, c, not_3_out);
  and and_4 (and_4_out, not_2_out, not_1_out, c, d);
  and and_5 (and_5_out, not_2_out, b, not_4_out, d);
  and and_6 (and_6_out, a, not_1_out, not_4_out, not_3_out);
  and and_7 (and_7_out, a, b, not_4_out, d);
  or or_1 (out_5, and_1_out, and_2_out, and_3_out, and_4_out, and_5_out, and_6_out, and_7_out);

  // Notes on the sheet:
  //   1a)
  //   806454 - Yago Almeida Melo
endmodule
