// Logisim project R01_01b.circ as structural Verilog: 1 circuit, main circuit main
module main (
  input  A,
  input  B,
  input  C,
  input  D,
  output out_5
);

  wire not_1_out, not_2_out, not_3_out, not_4_out, or_1_out, or_2_out, or_3_out, or_4_out, or_5_out,
       or_6_out, or_7_out, or_8_out, or_9_out;

  not not_1 (not_1_out, B);
  not not_2 (not_2_out, A);
  not not_3 (not_3_out, D);
  not not_4 (not_4_out, C);
  or or_1 (or_1_out, A, not_1_out, C, D);
  or or_2 (or_2_out, A, not_1_out, not_4_out, D);
  or or_3 (or_3_out, A, not_1_out, not_4_out, not_3_out);
  or or_4 (or_4_out, not_2_out, B, C, not_3_out);
  or or_5 (or_5_out, not_2_out, B, not_4_out, D);
  or or_6 (or_6_out, not_2_out, B, not_4_out, not_3_out);
  or or_7 (or_7_out, not_2_out, not_1_out, C, D);
  or or_8 (or_8_out, not_2_out, not_1_out, not_4_out, D);
  or or_9 (or_9_out, not_2_out, not_1_out, not_4_out, not_3_out);
  and and_1 (out_5, or_1_out, or_2_out, or_3_out, or_4_out, or_5_out, or_6_out, or_7_out, or_8_out, or_9_out);

  // Notes on the sheet:
  //   1b)
  //   806454 - Yago Almeida Melo
endmodule
