// Logisim project R01_01cd.circ as structural Verilog: 1 circuit, main circuit main
module main (
  input  a_A,
  input  b_B,
  input  c_C,
  input  d_D,
  output _1c,
  output _1d
);

  wire and_1_out, and_2_out, and_3_out, not_1_out, not_2_out, not_3_out, not_4_out, or_1_out, or_2_out,
       or_3_out, or_4_out;

  not not_1 (not_1_out, b_B);
  not not_2 (not_2_out, a_A);
  not not_3 (not_3_out, d_D);
  not not_4 (not_4_out, c_C);
  and and_1 (and_1_out, not_2_out, not_1_out);
  and and_2 (and_2_out, b_B, not_4_out, d_D);
  and and_3 (and_3_out, not_1_out, not_4_out, not_3_out);
  or or_1 (or_1_out, not_1_out, not_4_out);
  or or_2 (or_2_out, not_2_out, b_B, not_4_out);
  or or_3 (or_3_out, not_2_out, b_B, not_3_out);
  or or_4 (or_4_out, not_1_out, c_C, d_D);
  or or_5 (_1c, and_1_out, and_2_out, and_3_out);
  and and_4 (_1d, or_1_out, or_2_out, or_3_out, or_4_out);

  // Notes on the sheet:
  //   806454 - Yago Almeida Melo
endmodule
