// Logisim project R01_01ef.circ as structural Verilog: 1 circuit, main circuit main
module main (
  input  a,
  input  b,
  input  c,
  input  d,
  output out_5,
  output out_6
);

  wire nand_1_out, nand_2_out, nand_3_out, nand_4_out, nand_5_out, nand_6_out, nand_7_out, nand_8_out,
       nand_9_out, nor_1_out, nor_2_out, nor_3_out, nor_4_out, nor_5_out, nor_6_out, nor_7_out, nor_8_out,
       nor_9_out, nor_10_out, nor_11_out, nor_12_out, not_1_out, not_2_out, not_3_out, not_4_out;

  not not_1 (not_1_out, a);
  not not_2 (not_2_out, b);
  not not_3 (not_3_out, c);
  not not_4 (not_4_out, d);
  nand nand_1 (nand_1_out, not_1_out, not_2_out);
  nand nand_2 (nand_2_out, b, not_3_out, d);
  nand nand_3 (nand_3_out, not_2_out, not_3_out, not_4_out);
  nor nor_1 (nor_1_out, not_2_out, not_3_out);
  nor nor_2 (nor_2_out, not_1_out, b, not_3_out);
  nor nor_3 (nor_3_out, not_1_out, b, not_4_out);
  nor nor_4 (nor_4_out, not_2_out, c, d);
  nand nand_4 (nand_4_out, nand_1_out, nand_1_out);
  nand nand_5 (nand_5_out, nand_2_out, nand_2_out);
  nand nand_6 (nand_6_out, nand_3_out, nand_3_out);
  nor nor_5 (nor_5_out, nor_1_out, nor_1_out);
  nor nor_6 (nor_6_out, nor_2_out, nor_2_out);
  nor nor_7 (nor_7_out, nor_3_out, nor_3_out);
  nor nor_8 (nor_8_out, nor_4_out, nor_4_out);
  nand nand_7 (nand_7_out, nand_4_out, nand_4_out);
  nand nand_8 (nand_8_out, nand_5_out, nand_5_out);
  nand nand_9 (nand_9_out, nand_6_out, nand_6_out);
  nor nor_9 (nor_9_out, nor_5_out, nor_5_out);
  nor nor_10 (nor_10_out, nor_6_out, nor_6_out);
  nor nor_11 (nor_11_out, nor_7_out, nor_7_out);
  nor nor_12 (nor_12_out, nor_8_out, nor_8_out);
  nand nand_10 (out_5, nand_7_out, nand_8_out, nand_9_out);
  nor nor_13 (out_6, nor_9_out, nor_10_out, nor_11_out, nor_12_out);

  // Notes on the sheet:
  //   806454 - Yago Almeida Melo
  //   1e)
  //   1f)
endmodule
