// Logisim project R01_02.circ as structural Verilog: 1 circuit, main circuit main
module main (
  input  x,
  input  y,
  output _2
);

  wire and_1_out, not_1_out, not_2_out, or_1_out;

  not not_1 (not_1_out, y);
  and and_1 (and_1_out, not_1_out, x);
  or or_1 (or_1_out, x, y);
  not not_2 (not_2_out, and_1_out);
  or or_2 (_2, not_2_out, or_1_out);

  // Notes on the sheet:
  //   806454 - Yago Almeida Melo
endmodule
