// Logisim project R01_03ab.circ as structural Verilog: 1 circuit, main circuit main
module main (
  input  a,
  input  b,
  input  c,
  input  d,
  output _3a,
  output _3b
);

  wire multiplexer_1_out, multiplexer_2_out, nand_1_out, nand_2_out, not_1_out, not_2_out, not_3_out;

  nand nand_1 (nand_1_out, a, c);
  nand nand_2 (nand_2_out, b, d);
  Multiplexer #(.enable("false")) multiplexer_1 (.in0(b), .in1(c), .out(multiplexer_1_out), .sel(a));
  not not_1 (not_1_out, a);
  Multiplexer #(.enable("false")) multiplexer_2 (.in0(not_1_out), .in1(not_2_out), .out(multiplexer_2_out), .sel(c));
  not not_2 (not_2_out, b);
  nand nand_3 (_3a, nand_1_out, nand_2_out);
  Multiplexer #(.enable("false")) multiplexer_3 (
    .in0(multiplexer_1_out), .in1(multiplexer_2_out), .out(_3b), .sel(not_3_out));
  not not_3 (not_3_out, c);

  // Notes on the sheet:
  //   806454 - Yago Almeida Melo
endmodule
