// Logisim project R01_05.circ as structural Verilog: 1 circuit, main circuit main
module main (
  input  [5:0] in_1,
  input  [5:0] in_2,
  output [5:0] out_3,
  output [5:0] out_4
);

  wire [5:0] not_1_out, not_2_out;

  assign out_3 = in_1 ^ in_2;  // XOR_Gate xor_1, 6 bits wide
  assign not_1_out = ~in_1;  // NOT_Gate not_1, 6 bits wide
  assign not_2_out = ~in_2;  // NOT_Gate not_2, 6 bits wide
  assign out_4 = not_1_out ^ not_2_out;  // XOR_Gate xor_2, 6 bits wide

  // Notes on the sheet:
  //   806454 - Yago Almeida Melo
endmodule
