// Logisim project R02-04a.circ as structural Verilog: 1 circuit, main circuit main
module main (
  input  a,
  input  b,
  input  c,
  input  in_4,
  output out_5
);

  wire and_1_out, and_2_out, not_1_out, not_2_out, or_1_out;

  not not_1 (not_1_out, b);
  not not_2 (not_2_out, c);
  and and_1 (and_1_out, c, not_1_out);
  or or_1 (or_1_out, and_1_out, and_2_out);
  and and_2 (and_2_out, a, not_2_out);
  D_Flip_Flop d_ff_1 (.clk(in_4), .D(or_1_out), .Q(out_5));  // open: Qn, preset, reset

  // Notes on the sheet:
  //   806454 - Yago Almeida Melo
endmodule
