// Logisim project R02-04c.circ as structural Verilog: 1 circuit, main circuit main
module main (
  input  a,
  input  b,
  input  c,
  input  CLK,
  output out_5
);

  wire and_1_out, and_2_out, not_1_out, not_2_out, not_3_out, or_1_out;

  not not_1 (not_1_out, a);
  not not_2 (not_2_out, c);
  not not_3 (not_3_out, b);
  and and_1 (and_1_out, not_1_out, b, c);
  and and_2 (and_2_out, a, not_3_out, c);
  or or_1 (or_1_out, and_1_out, and_2_out);
  T_Flip_Flop t_ff_1 (.clk(CLK), .T(or_1_out), .Q(out_5));  // open: Qn, preset, reset

  // Notes on the sheet:
  //   806454 - Yago Almeida Melo
endmodule
