// Logisim project R02-04d.circ as structural Verilog: 1 circuit, main circuit main
module main (
  input  a,
  input  b,
  input  c,
  input  in_4,
  output out_5
);

  wire and_1_out, and_2_out, not_1_out, not_2_out, not_3_out;

  not not_1 (not_1_out, a);
  not not_2 (not_2_out, b);
  not not_3 (not_3_out, c);
  and and_1 (and_1_out, not_1_out, not_2_out, c);
  and and_2 (and_2_out, a, b, c);
  S_R_Flip_Flop s_r_ff_1 (.S(and_1_out), .clk(in_4), .R(and_2_out), .Q(out_5));  // open: Qn, preset, reset

  // Notes on the sheet:
  //   806454 - Yago Almeida Melo
endmodule
