// Logisim project R02-05d.circ as structural Verilog: 1 circuit, main circuit main
module main (
  input  CLK,
  input  CLEAR,
  output a,
  output b,
  output c,
  output d
);

  wire nand_1_out;

  D_Flip_Flop #(.Pre_Clr_Positions("LEGACY"), .enable("true"), .NewFFLayout("false")) d_ff_1 (
    .clk(CLK), .D(nand_1_out), .Q(a), .reset(CLEAR));  // open: Qn, preset, en
  nand nand_1 (nand_1_out, 1'b0, d);
  D_Flip_Flop #(.Pre_Clr_Positions("LEGACY"), .enable("true"), .NewFFLayout("false")) d_ff_2 (
    .clk(CLK), .D(a), .Q(b), .reset(CLEAR));  // open: Qn, preset, en
  D_Flip_Flop #(.Pre_Clr_Positions("LEGACY"), .enable("true"), .NewFFLayout("false")) d_ff_3 (
    .clk(CLK), .D(b), .Q(c), .reset(CLEAR));  // open: Qn, preset, en
  D_Flip_Flop #(.Pre_Clr_Positions("LEGACY"), .enable("true"), .NewFFLayout("false")) d_ff_4 (
    .clk(CLK), .D(c), .Q(d), .reset(CLEAR));  // open: Qn, preset, en

  // Notes on the sheet:
  //   806454 - Yago Almeida Melo
endmodule
