// Logisim project R02-05eee.circ as structural Verilog: 1 circuit, main circuit main
module main (
  input  CLK,
  input  CLEAR,
  output a,
  output b,
  output c,
  output d
);

  wire d_ff_1_qn, d_ff_2_qn, d_ff_3_qn, d_ff_4_qn;

  D_Flip_Flop #(.Pre_Clr_Positions("LEGACY"), .enable("true"), .NewFFLayout("false")) d_ff_1 (
    .clk(CLK), .D(d_ff_4_qn), .Q(a), .Qn(d_ff_1_qn), .reset(CLEAR));  // open: preset, en
  D_Flip_Flop #(.Pre_Clr_Positions("LEGACY"), .enable("true"), .NewFFLayout("false")) d_ff_2 (
    .clk(CLK), .D(d_ff_1_qn), .Q(b), .Qn(d_ff_2_qn), .reset(CLEAR));  // open: preset, en
  D_Flip_Flop #(.Pre_Clr_Positions("LEGACY"), .enable("true"), .NewFFLayout("false")) d_ff_3 (
    .clk(CLK), .D(d_ff_2_qn), .Q(c), .Qn(d_ff_3_qn), .reset(CLEAR));  // open: preset, en
  D_Flip_Flop #(.Pre_Clr_Positions("LEGACY"), .enable("true"), .NewFFLayout("false")) d_ff_4 (
    .clk(CLK), .D(d_ff_3_qn), .Q(d), .Qn(d_ff_4_qn), .reset(CLEAR));  // open: preset, en

  // Notes on the sheet:
  //   806454 - Yago Almeida Melo
endmodule
