// Logisim project R02-06.circ as structural Verilog: 1 circuit, main circuit main
module main (
  input  CLK,
  input  IN,
  output out_3
);

  wire and_1_out, and_2_out, d_ff_1_q, d_ff_1_qn, d_ff_2_q, d_ff_2_qn, d_ff_3_q, d_ff_3_qn;

  D_Flip_Flop d_ff_1 (.clk(CLK), .D(IN), .Q(d_ff_1_q), .Qn(d_ff_1_qn));  // open: preset, reset
  D_Flip_Flop d_ff_2 (.clk(CLK), .D(d_ff_1_q), .Q(d_ff_2_q), .Qn(d_ff_2_qn));  // open: preset, reset
  and and_1 (and_1_out, d_ff_3_q, d_ff_2_q, d_ff_1_q);
  and and_2 (and_2_out, d_ff_3_qn, d_ff_2_qn, d_ff_1_qn);
  or or_1 (out_3, and_1_out, and_2_out);
  D_Flip_Flop d_ff_3 (.clk(CLK), .D(d_ff_2_q), .Q(d_ff_3_q), .Qn(d_ff_3_qn));  // open: preset, reset

  // Notes on the sheet:
  //   806454 - Yago Almeida Melo
endmodule
