// Logisim project Somadores.circ as structural Verilog: 4 circuits, main circuit main
module main (
  input  x,
  input  y,
  output soma,
  output carry_out
);

  xor xor_1 (soma, x, y);
  and and_1 (carry_out, x, y);
endmodule

module Half_Adder (
  input  x,
  input  y,
  output soma,
  output carry_out
);

  xor xor_1 (soma, x, y);
  and and_1 (carry_out, x, y);
endmodule

module Full_Adder (
  input  A,
  input  B,
  input  Ci,
  output S,
  output Co
);

  wire half_adder_1_carry_out, half_adder_1_soma, half_adder_2_carry_out;

  Half_Adder half_adder_1 (.x(A), .y(B), .soma(half_adder_1_soma), .carry_out(half_adder_1_carry_out));
  Half_Adder half_adder_2 (.x(half_adder_1_soma), .y(Ci), .soma(S), .carry_out(half_adder_2_carry_out));
  or or_1 (Co, half_adder_2_carry_out, half_adder_1_carry_out);
endmodule

module Somador_4bits (
  input  [3:0] A,
  input  [3:0] B,
  output [3:0] Saida,
  output overflow
);

  wire full_adder_1_co, full_adder_2_co, full_adder_3_co;

  Full_Adder full_adder_1 (.A(A[0]), .B(B[0]), .Ci(1'b0), .S(Saida[0]), .Co(full_adder_1_co));
  Full_Adder full_adder_2 (.A(A[1]), .B(B[1]), .Ci(full_adder_1_co), .S(Saida[1]), .Co(full_adder_2_co));
  Full_Adder full_adder_3 (.A(A[2]), .B(B[2]), .Ci(full_adder_2_co), .S(Saida[2]), .Co(full_adder_3_co));
  Full_Adder full_adder_4 (.A(A[3]), .B(B[3]), .Ci(full_adder_3_co), .S(Saida[3]), .Co(overflow));
endmodule
