// Logisim project calculadora-4bits.circ as structural Verilog: 5 circuits, main circuit Calculadora 4bits
module Calculadora_4bits (
  input  Vem1,
  input  x3,
  input  x2,
  input  x1,
  input  x0,
  input  y3,
  input  y2,
  input  y1,
  input  y0,
  output out_10,
  output out_11,
  output out_12,
  output out_13,
  output out_14
);

  wire Decodificador_2_a, Decodificador_2_b, Decodificador_2_c, Decodificador_2_d, Decodificador_2_e,
       Decodificador_2_f, Decodificador_2_g, Decodificador_3_a, Decodificador_3_b, Decodificador_3_c,
       Decodificador_3_d, Decodificador_3_e, Decodificador_3_f, Decodificador_3_g, Decodificador_a,
       Decodificador_b, Decodificador_c, Decodificador_d, Decodificador_e, Decodificador_f, Decodificador_g;

  Decodificador Decodificador (
    .e0(x3), .e1(x2), .e2(x1), .e3(x0), .a(Decodificador_a), .b(Decodificador_b), .c(Decodificador_c),
    .d(Decodificador_d), .e(Decodificador_e), .f(Decodificador_f), .g(Decodificador_g));
  Somador_4bits Somador_4bits (
    .x3(x3), .x2(x2), .x1(x1), .x0(x0), .y3(y3), .y2(y2), .y1(y1), .y0(y0), .in_1(Vem1), .out_14(out_14),
    .s0(out_10), .s1(out_11), .s2(out_12), .s3(out_13));
  Decodificador Decodificador_2 (
    .e0(y3), .e1(y2), .e2(y1), .e3(y0), .a(Decodificador_2_a), .b(Decodificador_2_b), .c(Decodificador_2_c),
    .d(Decodificador_2_d), .e(Decodificador_2_e), .f(Decodificador_2_f), .g(Decodificador_2_g));
  _7_Segment_Display u_7_segment_display_1 (
    .g(Decodificador_g), .f(Decodificador_f), .a(Decodificador_a), .b(Decodificador_b), .e(Decodificador_e),
    .d(Decodificador_d), .c(Decodificador_c));  // open: dp
  _7_Segment_Display u_7_segment_display_2 (
    .g(Decodificador_2_g), .f(Decodificador_2_f), .a(Decodificador_2_a), .b(Decodificador_2_b),
    .e(Decodificador_2_e), .d(Decodificador_2_d), .c(Decodificador_2_c));  // open: dp
  Decodificador Decodificador_3 (
    .e0(out_13), .e1(out_12), .e2(out_11), .e3(out_10), .a(Decodificador_3_a), .b(Decodificador_3_b),
    .c(Decodificador_3_c), .d(Decodificador_3_d), .e(Decodificador_3_e), .f(Decodificador_3_f),
    .g(Decodificador_3_g));
  _7_Segment_Display u_7_segment_display_3 (
    .g(Decodificador_3_g), .f(Decodificador_3_f), .a(Decodificador_3_a), .b(Decodificador_3_b),
    .e(Decodificador_3_e), .d(Decodificador_3_d), .c(Decodificador_3_c));  // open: dp

  // Notes on the sheet:
  //   806454 - Yago Almeida Melo
endmodule

module Meio_somador (
  input  x,
  input  y,
  output s,
  output vai1
);

  and and_1 (vai1, x, y);
  xor xor_1 (s, x, y);

  // Notes on the sheet:
  //   806454 - Yago Almeida Melo
endmodule

module Somador_completo (
  input  vem1,
  input  x,
  input  y,
  output S,
  output vai1
);

  wire meio_somador_1_s, meio_somador_1_vai1, meio_somador_2_vai1;

  Meio_somador meio_somador_1 (.x(x), .y(y), .vai1(meio_somador_1_vai1), .s(meio_somador_1_s));
  or or_1 (vai1, meio_somador_1_vai1, meio_somador_2_vai1);
  Meio_somador meio_somador_2 (.x(vem1), .y(meio_somador_1_s), .vai1(meio_somador_2_vai1), .s(S));

  // Notes on the sheet:
  //   806454 - Yago Almeida Melo
endmodule

module Somador_4bits (
  input  in_1,
  input  x3,
  input  x2,
  input  x1,
  input  x0,
  input  y3,
  input  y2,
  input  y1,
  input  y0,
  output s0,
  output s1,
  output s2,
  output s3,
  output out_14
);

  wire somador_completo_1_vai1, somador_completo_2_vai1, somador_completo_3_vai1;

  Somador_completo somador_completo_1 (.x(x0), .y(y0), .vem1(in_1), .vai1(somador_completo_1_vai1), .S(s0));
  Somador_completo somador_completo_2 (
    .x(x1), .y(y1), .vem1(somador_completo_1_vai1), .vai1(somador_completo_2_vai1), .S(s1));
  Somador_completo somador_completo_3 (
    .x(x2), .y(y2), .vem1(somador_completo_2_vai1), .vai1(somador_completo_3_vai1), .S(s2));
  Somador_completo somador_completo_4 (.x(x3), .y(y3), .vem1(somador_completo_3_vai1), .vai1(out_14), .S(s3));

  // Notes on the sheet:
  //   806454 - Yago Almeida Melo
endmodule

module Decodificador (
  input  e0,
  input  e1,
  input  e2,
  input  e3,
  output a,
  output b,
  output c,
  output d,
  output e,
  output f,
  output g
);

  wire and_1_out, and_2_out, and_3_out, and_4_out, and_5_out, and_6_out, and_7_out, and_8_out, and_9_out,
       and_10_out, and_11_out, and_12_out, and_13_out, and_14_out, and_15_out, and_16_out, and_17_out,
       and_18_out, and_19_out, and_20_out, and_21_out, and_22_out, and_23_out, and_24_out, and_25_out,
       and_26_out, and_27_out, and_28_out, and_29_out, and_30_out, and_31_out, and_32_out, and_33_out,
       and_34_out, and_35_out, not_1_out, not_2_out, not_3_out, not_4_out, not_5_out, not_6_out, not_7_out,
       not_8_out, not_9_out, not_10_out, not_11_out, not_12_out, not_13_out, not_14_out, not_15_out,
       not_16_out, not_17_out, not_18_out, not_19_out, not_20_out, not_21_out, not_22_out, not_23_out,
       not_24_out, not_25_out, not_26_out, not_27_out, not_28_out, not_29_out, not_30_out, not_31_out,
       not_32_out, not_33_out, not_34_out, not_35_out, not_36_out, not_37_out, not_38_out, not_39_out,
       not_40_out, not_41_out, not_42_out, not_43_out;

  not not_1 (not_1_out, e1);
  and and_1 (and_1_out, not_1_out, not_2_out);
  not not_2 (not_2_out, e3);
  not not_3 (not_3_out, e0);
  and and_2 (and_2_out, not_3_out, e2);
  not not_4 (not_4_out, e0);
  and and_3 (and_3_out, not_4_out, e1, e3);
  and and_4 (and_4_out, e1, e2);
  and and_5 (and_5_out, e0, not_5_out, not_6_out);
  not not_5 (not_5_out, e1);
  not not_6 (not_6_out, e2);
  and and_6 (and_6_out, e0, not_7_out);
  not not_7 (not_7_out, e3);
  not not_8 (not_8_out, e0);
  and and_7 (and_7_out, not_8_out, not_9_out);
  not not_9 (not_9_out, e1);
  not not_10 (not_10_out, e0);
  and and_8 (and_8_out, not_10_out, not_11_out, not_12_out);
  not not_11 (not_11_out, e2);
  not not_12 (not_12_out, e3);
  not not_13 (not_13_out, e1);
  and and_9 (and_9_out, not_13_out, not_14_out);
  not not_14 (not_14_out, e3);
  not not_15 (not_15_out, e0);
  and and_10 (and_10_out, not_15_out, e2, e3);
  not not_16 (not_16_out, e2);
  and and_11 (and_11_out, e0, not_16_out, e3);
  not not_17 (not_17_out, e0);
  and and_12 (and_12_out, not_17_out, not_18_out);
  not not_18 (not_18_out, e2);
  not not_19 (not_19_out, e0);
  and and_13 (and_13_out, not_19_out, e3);
  not not_20 (not_20_out, e2);
  and and_14 (and_14_out, not_20_out, e3);
  not not_21 (not_21_out, e0);
  and and_15 (and_15_out, not_21_out, e1);
  and and_16 (and_16_out, e0, not_22_out);
  not not_22 (not_22_out, e1);
  not not_23 (not_23_out, e0);
  not not_24 (not_24_out, e1);
  and and_17 (and_17_out, not_23_out, not_24_out, not_25_out);
  not not_25 (not_25_out, e3);
  not not_26 (not_26_out, e1);
  and and_18 (and_18_out, not_26_out, e2, e3);
  and and_19 (and_19_out, e1, not_27_out, e3);
  not not_27 (not_27_out, e2);
  and and_20 (and_20_out, e1, e2, not_28_out);
  not not_28 (not_28_out, e3);
  and and_21 (and_21_out, e0, not_29_out);
  not not_29 (not_29_out, e2);
  not not_30 (not_30_out, e1);
  and and_22 (and_22_out, not_30_out, not_31_out);
  not not_31 (not_31_out, e3);
  and and_23 (and_23_out, e2, not_32_out);
  not not_32 (not_32_out, e3);
  and and_24 (and_24_out, e0, e2);
  and and_25 (and_25_out, e0, e1);
  not not_33 (not_33_out, e2);
  and and_26 (and_26_out, not_33_out, not_34_out);
  not not_34 (not_34_out, e3);
  not not_35 (not_35_out, e0);
  and and_27 (and_27_out, not_35_out, e1, not_36_out);
  not not_36 (not_36_out, e2);
  and and_28 (and_28_out, e1, not_37_out);
  not not_37 (not_37_out, e3);
  and and_29 (and_29_out, e0, not_38_out);
  not not_38 (not_38_out, e1);
  and and_30 (and_30_out, e0, e2);
  not not_39 (not_39_out, e1);
  and and_31 (and_31_out, not_39_out, e2);
  and and_32 (and_32_out, e2, not_40_out);
  not not_40 (not_40_out, e3);
  not not_41 (not_41_out, e0);
  and and_33 (and_33_out, not_41_out, e1, not_42_out);
  not not_42 (not_42_out, e2);
  and and_34 (and_34_out, e0, not_43_out);
  not not_43 (not_43_out, e1);
  and and_35 (and_35_out, e0, e3);
  or or_1 (b, and_7_out, and_8_out, and_9_out, and_10_out, and_11_out);
  or or_2 (c, and_12_out, and_13_out, and_14_out, and_15_out, and_16_out);
  or or_3 (d, and_17_out, and_18_out, and_19_out, and_20_out, and_21_out);
  or or_4 (e, and_22_out, and_23_out, and_24_out, and_25_out);
  or or_5 (f, and_26_out, and_27_out, and_28_out, and_29_out, and_30_out);
  or or_6 (g, and_31_out, and_32_out, and_33_out, and_34_out, and_35_out);
  or or_7 (a, and_1_out, and_2_out, and_3_out, and_4_out, and_5_out, and_6_out);
endmodule
