// Logisim project Circuitos.circ as structural Verilog
module main (
  input  in_1,
  input  in_2,
  input  in_3,
  output out_4
);

  wire and_1_out, and_2_out, not_1_out;

  not not_1 (not_1_out, in_1);
  and and_1 (and_1_out, in_2, not_1_out);
  and and_2 (and_2_out, in_3, in_1);
  or or_1 (out_4, and_1_out, and_2_out);

  // Notes on the sheet:
  //   806454 - Yago Almeida
endmodule

module Mux_1bit (
  input  in_1,
  input  in_2,
  input  in_3,
  output out_4
);

  wire and_1_out, and_2_out, not_1_out;

  not not_1 (not_1_out, in_1);
  and and_1 (and_1_out, in_2, not_1_out);
  and and_2 (and_2_out, in_3, in_1);
  or or_1 (out_4, and_1_out, and_2_out);

  // Notes on the sheet:
  //   806454 - Yago Almeida
endmodule

module ULA_1bit (
  input  in_1,
  input  in_2,
  input  in_3
);

  // AND_Gate and_1 is placed but not wired
endmodule

module FULL_ADDER (
  input  a,
  input  b,
  input  CarryIn,
  output out_4,
  output out_5
);

  wire and_1_out, and_2_out, xor_1_out;

  xor xor_1 (xor_1_out, a, b);
  and and_1 (and_1_out, a, b);
  xor xor_2 (out_4, xor_1_out, CarryIn);
  and and_2 (and_2_out, xor_1_out, CarryIn);
  or or_1 (out_5, and_2_out, and_1_out);
endmodule
